// Logisim project 4_ENCODER.circ as structural Verilog: 2 circuits, main circuit main
module main (
  input  [15:0] in_1
);

  wire n4_bits_7_seg_display_1_y0, n4_bits_7_seg_display_1_y1, n4_bits_7_seg_display_1_y2,
       n4_bits_7_seg_display_1_y3, n4_bits_7_seg_display_1_y4, n4_bits_7_seg_display_1_y5,
       n4_bits_7_seg_display_1_y6, n4_bits_7_seg_display_1_y7, n16_4_encoder_1_y0, n16_4_encoder_1_y1,
       n16_4_encoder_1_y2, n16_4_encoder_1_y3;

  _16_4_ENCODER u_16_4_encoder_1 (
    .A15(in_1[15]), .A14(in_1[14]), .A13(in_1[13]), .A12(in_1[12]), .A11(in_1[11]), .A10(in_1[10]),
    .A9(in_1[9]), .A8(in_1[8]), .A7(in_1[7]), .A6(in_1[6]), .A5(in_1[5]), .A4(in_1[4]), .A3(in_1[3]),
    .A2(in_1[2]), .A1(in_1[1]), .A0(in_1[0]), .Y3(n16_4_encoder_1_y3), .Y2(n16_4_encoder_1_y2),
    .Y1(n16_4_encoder_1_y1), .Y0(n16_4_encoder_1_y0));
  _4_bits_7_seg_display u_4_bits_7_seg_display_1 (
    .In3(n16_4_encoder_1_y3), .In2(n16_4_encoder_1_y2), .In1(n16_4_encoder_1_y1), .In0(n16_4_encoder_1_y0),
    .Y0(n4_bits_7_seg_display_1_y0), .Y1(n4_bits_7_seg_display_1_y1), .Y2(n4_bits_7_seg_display_1_y2),
    .Y3(n4_bits_7_seg_display_1_y3), .Y4(n4_bits_7_seg_display_1_y4), .Y5(n4_bits_7_seg_display_1_y5),
    .Y6(n4_bits_7_seg_display_1_y6), .Y7(n4_bits_7_seg_display_1_y7));
  _7_Segment_Display u_7_segment_display_1 (
    .g(n4_bits_7_seg_display_1_y0), .f(n4_bits_7_seg_display_1_y1), .a(n4_bits_7_seg_display_1_y2),
    .b(n4_bits_7_seg_display_1_y3), .e(n4_bits_7_seg_display_1_y4), .d(n4_bits_7_seg_display_1_y5),
    .c(n4_bits_7_seg_display_1_y6), .dp(n4_bits_7_seg_display_1_y7));
endmodule

module _16_4_ENCODER (
  input  A15,
  input  A14,
  input  A13,
  input  A12,
  input  A11,
  input  A10,
  input  A9,
  input  A8,
  input  A7,
  input  A6,
  input  A5,
  input  A4,
  input  A3,
  input  A2,
  input  A1,
  input  A0,
  output Y3,
  output Y2,
  output Y1,
  output Y0
);

  or or_1 (Y3, A15, A14, A13, A12, A11, A10, A9, A8);
  or or_2 (Y2, A15, A5, A14, A4, A7, A13, A6, A12);
  or or_3 (Y1, A15, A14, A11, A10, A7, A6, A3, A2);
  or or_4 (Y0, A15, A13, A11, A9, A7, A5, A3, A1);
  // also tied to GND on the sheet: A0
endmodule
