// Logisim project 4_Pri_Encoder_display.circ as structural Verilog: 2 circuits, main circuit main
module main (
  input  [15:0] in_1
);

  wire n4_bits_7_seg_display_1_y0, n4_bits_7_seg_display_1_y1, n4_bits_7_seg_display_1_y2,
       n4_bits_7_seg_display_1_y3, n4_bits_7_seg_display_1_y4, n4_bits_7_seg_display_1_y5,
       n4_bits_7_seg_display_1_y6, n4_bits_7_seg_display_1_y7, n16_4_pri_encoder_1_y0,
       n16_4_pri_encoder_1_y1, n16_4_pri_encoder_1_y2, n16_4_pri_encoder_1_y3;

  _16_4_Pri_Encoder u_16_4_pri_encoder_1 (
    .in_1(in_1), .Y3(n16_4_pri_encoder_1_y3), .Y2(n16_4_pri_encoder_1_y2), .Y1(n16_4_pri_encoder_1_y1),
    .Y0(n16_4_pri_encoder_1_y0));
  _4_bits_7_seg_display u_4_bits_7_seg_display_1 (
    .In3(n16_4_pri_encoder_1_y3), .In2(n16_4_pri_encoder_1_y2), .In1(n16_4_pri_encoder_1_y1),
    .In0(n16_4_pri_encoder_1_y0), .Y0(n4_bits_7_seg_display_1_y0), .Y1(n4_bits_7_seg_display_1_y1),
    .Y2(n4_bits_7_seg_display_1_y2), .Y3(n4_bits_7_seg_display_1_y3), .Y4(n4_bits_7_seg_display_1_y4),
    .Y5(n4_bits_7_seg_display_1_y5), .Y6(n4_bits_7_seg_display_1_y6), .Y7(n4_bits_7_seg_display_1_y7));
  _7_Segment_Display u_7_segment_display_1 (
    .g(n4_bits_7_seg_display_1_y0), .f(n4_bits_7_seg_display_1_y1), .a(n4_bits_7_seg_display_1_y2),
    .b(n4_bits_7_seg_display_1_y3), .e(n4_bits_7_seg_display_1_y4), .d(n4_bits_7_seg_display_1_y5),
    .c(n4_bits_7_seg_display_1_y6), .dp(n4_bits_7_seg_display_1_y7));
endmodule

module _16_4_Pri_Encoder (
  input  [15:0] in_1,
  output Y3,
  output Y2,
  output Y1,
  output Y0
);

  wire [7:0] multiplexer_1_out;

  or or_1 (Y3, in_1[15], in_1[14], in_1[13], in_1[12], in_1[11], in_1[10], in_1[9], in_1[8]);
  Multiplexer #(.width(8), .enable("false")) multiplexer_1 (
    .in0(in_1[7:0]), .in1(in_1[15:8]), .out(multiplexer_1_out), .sel(Y3));
  _8_3_Pri_Encoder u_8_3_pri_encoder_1 (.in_1(multiplexer_1_out), .Y2(Y2), .Y1(Y1), .Y0(Y0));
endmodule
