// Logisim project 4_DECODER.circ as structural Verilog: 1 circuit, main circuit main
module main (
  input  E,
  input  In1,
  input  In0,
  output Y3,
  output Y2,
  output Y1,
  output Y0
);

  wire not_1_out, not_2_out;

  not not_1 (not_1_out, In1);
  not not_2 (not_2_out, In0);
  and and_1 (Y3, E, In1, In0);
  and and_2 (Y2, E, In1, not_2_out);
  and and_3 (Y1, E, not_1_out, In0);
  and and_4 (Y0, E, not_1_out, not_2_out);
endmodule
