// Logisim project 8_DECODER.circ as structural Verilog
module _3_8_DECODER (
  input  E,
  input  S2,
  input  S1,
  input  S0,
  output Y7,
  output Y6,
  output Y5,
  output Y4,
  output Y3,
  output Y2,
  output Y1,
  output Y0
);

  wire and_1_out, and_2_out, and_3_out, and_4_out, and_5_out, and_6_out, not_1_out;

  not not_1 (not_1_out, S2);
  and and_1 (and_1_out, E, S2);
  and and_2 (and_2_out, E, S1);
  and and_3 (and_3_out, E, S0);
  and and_4 (and_4_out, E, not_1_out);
  and and_5 (and_5_out, E, S1);
  and and_6 (and_6_out, E, S0);
  _4_DECODER_main main_1 (.E(and_1_out), .In1(and_2_out), .In0(and_3_out), .Y3(Y7), .Y2(Y6), .Y1(Y5), .Y0(Y4));
  _4_DECODER_main main_2 (.E(and_4_out), .In1(and_5_out), .In0(and_6_out), .Y3(Y3), .Y2(Y2), .Y1(Y1), .Y0(Y0));
endmodule
