// Logisim project 1_MUX.circ as structural Verilog
module _2_1_MUX (
  input  x,
  input  y,
  input  sel,
  output z
);

  wire and_1_out, and_2_out, not_1_out;

  not not_1 (not_1_out, sel);
  and and_1 (and_1_out, x, not_1_out);
  and and_2 (and_2_out, sel, y);
  or or_1 (z, and_1_out, and_2_out);
endmodule

module _4_1_MUX (
  input  w,
  input  x,
  input  y,
  input  z,
  input  sel0,
  input  sel1,
  output out
);

  wire n2_1_mux_1_z, n2_1_mux_2_z;

  _2_1_MUX u_2_1_mux_1 (.x(w), .y(x), .sel(sel0), .z(n2_1_mux_1_z));
  _2_1_MUX u_2_1_mux_2 (.x(y), .y(z), .sel(sel0), .z(n2_1_mux_2_z));
  _2_1_MUX u_2_1_mux_3 (.x(n2_1_mux_1_z), .y(n2_1_mux_2_z), .sel(sel1), .z(out));
endmodule
