// Logisim project 1_MUX3.circ as structural Verilog
module _2_1_MUX3 (
  input  [2:0] I1,
  input  [2:0] I0,
  input  sel,
  output [2:0] O
);

  wire and_1_out, and_2_out, and_3_out, and_4_out, and_5_out, and_6_out, not_1_out;

  not not_1 (not_1_out, sel);
  and and_1 (and_1_out, I1[0], sel);
  and and_2 (and_2_out, I1[1], sel);
  and and_3 (and_3_out, I1[2], sel);
  and and_4 (and_4_out, I0[0], not_1_out);
  and and_5 (and_5_out, I0[1], not_1_out);
  and and_6 (and_6_out, I0[2], not_1_out);
  or or_1 (O[0], and_1_out, and_4_out);
  or or_2 (O[1], and_2_out, and_5_out);
  or or_3 (O[2], and_3_out, and_6_out);
endmodule

module _4_1_MUX3 (
  input  [2:0] I3,
  input  [2:0] I2,
  input  [2:0] I1,
  input  [2:0] I0,
  input  [1:0] sel,
  output [2:0] out_6
);

  wire [2:0] n2_1_mux3_1_o, n2_1_mux3_2_o;

  _2_1_MUX3 u_2_1_mux3_1 (.I1(I3), .I0(I2), .sel(sel[0]), .O(n2_1_mux3_1_o));
  _2_1_MUX3 u_2_1_mux3_2 (.I1(I1), .I0(I0), .sel(sel[0]), .O(n2_1_mux3_2_o));
  _2_1_MUX3 u_2_1_mux3_3 (.I1(n2_1_mux3_1_o), .I0(n2_1_mux3_2_o), .sel(sel[1]), .O(out_6));
endmodule
