// Logisim project 2_Pri_Encoder.circ as structural Verilog: 1 circuit, main circuit main
module main (
  input  A3,
  input  A2,
  input  A1,
  input  A0,
  output Y1,
  output Y0
);

  wire and_1_out, not_1_out;

  not not_1 (not_1_out, A2);
  and and_1 (and_1_out, not_1_out, A1);
  or or_1 (Y1, A3, A2);
  or or_2 (Y0, A3, and_1_out);
  // also tied to GND on the sheet: A0
endmodule
