// Logisim project 2_Pri_Encoder_display.circ as structural Verilog: 2 circuits, main circuit main
module main (
  input  [3:0] in_1
);

  wire n4_2_pri_encoder_1_y0, n4_2_pri_encoder_1_y1, n4_bits_7_seg_display_1_y0, n4_bits_7_seg_display_1_y1,
       n4_bits_7_seg_display_1_y2, n4_bits_7_seg_display_1_y3, n4_bits_7_seg_display_1_y4,
       n4_bits_7_seg_display_1_y5, n4_bits_7_seg_display_1_y6, n4_bits_7_seg_display_1_y7;

  _4_2_Pri_Encoder u_4_2_pri_encoder_1 (
    .A3(in_1[3]), .A2(in_1[2]), .A1(in_1[1]), .A0(in_1[0]), .Y1(n4_2_pri_encoder_1_y1),
    .Y0(n4_2_pri_encoder_1_y0));
  _4_bits_7_seg_display u_4_bits_7_seg_display_1 (
    .In3(1'b0), .In2(1'b0), .In1(n4_2_pri_encoder_1_y1), .In0(n4_2_pri_encoder_1_y0),
    .Y0(n4_bits_7_seg_display_1_y0), .Y1(n4_bits_7_seg_display_1_y1), .Y2(n4_bits_7_seg_display_1_y2),
    .Y3(n4_bits_7_seg_display_1_y3), .Y4(n4_bits_7_seg_display_1_y4), .Y5(n4_bits_7_seg_display_1_y5),
    .Y6(n4_bits_7_seg_display_1_y6), .Y7(n4_bits_7_seg_display_1_y7));
  _7_Segment_Display u_7_segment_display_1 (
    .g(n4_bits_7_seg_display_1_y0), .f(n4_bits_7_seg_display_1_y1), .a(n4_bits_7_seg_display_1_y2),
    .b(n4_bits_7_seg_display_1_y3), .e(n4_bits_7_seg_display_1_y4), .d(n4_bits_7_seg_display_1_y5),
    .c(n4_bits_7_seg_display_1_y6), .dp(n4_bits_7_seg_display_1_y7));
endmodule

module _4_2_Pri_Encoder (
  input  A3,
  input  A2,
  input  A1,
  input  A0,
  output Y1,
  output Y0
);

  wire and_1_out, not_1_out;

  not not_1 (not_1_out, A2);
  and and_1 (and_1_out, not_1_out, A1);
  or or_1 (Y1, A3, A2);
  or or_2 (Y0, A3, and_1_out);
  // also tied to GND on the sheet: A0
endmodule
