// Logisim project 4_bits_7_seg.circ as structural Verilog
module _4_bits_7_seg_display (
  input  In3,
  input  In2,
  input  In1,
  input  In0,
  output Y0,
  output Y1,
  output Y2,
  output Y3,
  output Y4,
  output Y5,
  output Y6,
  output Y7
);

  wire n3_8_decoder_1_y0, n3_8_decoder_1_y1, n3_8_decoder_1_y2, n3_8_decoder_1_y3, n3_8_decoder_1_y4,
       n3_8_decoder_1_y5, n3_8_decoder_1_y6, n3_8_decoder_1_y7, n3_8_decoder_2_y0, n3_8_decoder_2_y1,
       n3_8_decoder_2_y2, n3_8_decoder_2_y3, n3_8_decoder_2_y4, n3_8_decoder_2_y5, n3_8_decoder_2_y6,
       n3_8_decoder_2_y7, not_1_out;

  not not_1 (not_1_out, In3);
  _3_8_DECODER u_3_8_decoder_1 (
    .E(In3), .S2(In2), .S1(In1), .S0(In0), .Y7(n3_8_decoder_1_y7), .Y6(n3_8_decoder_1_y6),
    .Y5(n3_8_decoder_1_y5), .Y4(n3_8_decoder_1_y4), .Y3(n3_8_decoder_1_y3), .Y2(n3_8_decoder_1_y2),
    .Y1(n3_8_decoder_1_y1), .Y0(n3_8_decoder_1_y0));
  _3_8_DECODER u_3_8_decoder_2 (
    .E(not_1_out), .S2(In2), .S1(In1), .S0(In0), .Y7(n3_8_decoder_2_y7), .Y6(n3_8_decoder_2_y6),
    .Y5(n3_8_decoder_2_y5), .Y4(n3_8_decoder_2_y4), .Y3(n3_8_decoder_2_y3), .Y2(n3_8_decoder_2_y2),
    .Y1(n3_8_decoder_2_y1), .Y0(n3_8_decoder_2_y0));
  or or_1 (Y0, n3_8_decoder_1_y7, n3_8_decoder_1_y6, n3_8_decoder_1_y5, n3_8_decoder_1_y3, n3_8_decoder_1_y2, n3_8_decoder_1_y1, n3_8_decoder_1_y0, n3_8_decoder_2_y6, n3_8_decoder_2_y5, n3_8_decoder_2_y4, n3_8_decoder_2_y3, n3_8_decoder_2_y2);
  or or_2 (Y1, n3_8_decoder_1_y7, n3_8_decoder_1_y6, n3_8_decoder_1_y4, n3_8_decoder_1_y3, n3_8_decoder_1_y2, n3_8_decoder_1_y1, n3_8_decoder_1_y0, n3_8_decoder_2_y6, n3_8_decoder_2_y5, n3_8_decoder_2_y4, n3_8_decoder_2_y0);
  or or_3 (Y2, n3_8_decoder_1_y7, n3_8_decoder_1_y6, n3_8_decoder_1_y4, n3_8_decoder_1_y2, n3_8_decoder_1_y1, n3_8_decoder_1_y0, n3_8_decoder_2_y7, n3_8_decoder_2_y6, n3_8_decoder_2_y5, n3_8_decoder_2_y3, n3_8_decoder_2_y2, n3_8_decoder_2_y0);
  or or_4 (Y3, n3_8_decoder_1_y6, n3_8_decoder_1_y5, n3_8_decoder_1_y2, n3_8_decoder_1_y1, n3_8_decoder_1_y0, n3_8_decoder_2_y7, n3_8_decoder_2_y4, n3_8_decoder_2_y3, n3_8_decoder_2_y2, n3_8_decoder_2_y1, n3_8_decoder_2_y0);
  or or_5 (Y4, n3_8_decoder_1_y7, n3_8_decoder_1_y6, n3_8_decoder_1_y5, n3_8_decoder_1_y4, n3_8_decoder_1_y3, n3_8_decoder_1_y2, n3_8_decoder_1_y0, n3_8_decoder_2_y6, n3_8_decoder_2_y2, n3_8_decoder_2_y0);
  or or_6 (Y5, n3_8_decoder_1_y6, n3_8_decoder_1_y5, n3_8_decoder_1_y4, n3_8_decoder_1_y3, n3_8_decoder_1_y1, n3_8_decoder_1_y0, n3_8_decoder_2_y6, n3_8_decoder_2_y5, n3_8_decoder_2_y3, n3_8_decoder_2_y2, n3_8_decoder_2_y0);
  or or_7 (Y6, n3_8_decoder_1_y5, n3_8_decoder_1_y3, n3_8_decoder_1_y2, n3_8_decoder_1_y1, n3_8_decoder_1_y0, n3_8_decoder_2_y7, n3_8_decoder_2_y6, n3_8_decoder_2_y5, n3_8_decoder_2_y4, n3_8_decoder_2_y3, n3_8_decoder_2_y1, n3_8_decoder_2_y0);

  assign Y7 = 1'b0;
endmodule
