// Logisim project Comparator4.circ as structural Verilog: 1 circuit, main circuit main
module main (
  input  [3:0] in_1,
  input  [3:0] in_2
);

  wire and_1_out;
  wire [3:0] xnor_1_out;

  assign xnor_1_out = ~(in_1 ^ in_2);  // XNOR_Gate xnor_1, 4 bits wide
  LED led_1 (.in(and_1_out));
  and and_1 (and_1_out, xnor_1_out[0], xnor_1_out[1], xnor_1_out[2], xnor_1_out[3]);
endmodule
