// Logisim project Full_adder1.circ as structural Verilog: 1 circuit, main circuit main
module main (
  input  Cin,
  input  A,
  input  B,
  output Cout,
  output S
);

  wire n3_8_decoder_1_y1, n3_8_decoder_1_y2, n3_8_decoder_1_y3, n3_8_decoder_1_y4, n3_8_decoder_1_y5,
       n3_8_decoder_1_y6, n3_8_decoder_1_y7;

  _3_8_DECODER u_3_8_decoder_1 (
    .E(1'b1), .S2(Cin), .S1(A), .S0(B), .Y7(n3_8_decoder_1_y7), .Y6(n3_8_decoder_1_y6),
    .Y5(n3_8_decoder_1_y5), .Y4(n3_8_decoder_1_y4), .Y3(n3_8_decoder_1_y3), .Y2(n3_8_decoder_1_y2),
    .Y1(n3_8_decoder_1_y1));  // open: Y0
  or or_1 (Cout, n3_8_decoder_1_y7, n3_8_decoder_1_y6, n3_8_decoder_1_y5, n3_8_decoder_1_y3);
  or or_2 (S, n3_8_decoder_1_y7, n3_8_decoder_1_y4, n3_8_decoder_1_y2, n3_8_decoder_1_y1);
endmodule
