// Logisim project Full_adder4_display.circ as structural Verilog: 4 circuits, main circuit main
module main (
  input  [3:0] in_1,
  input  [3:0] in_2
);

  wire full_adder4_1_cout, n4_bits_7_seg_display_1_y0, n4_bits_7_seg_display_1_y1,
       n4_bits_7_seg_display_1_y2, n4_bits_7_seg_display_1_y3, n4_bits_7_seg_display_1_y4,
       n4_bits_7_seg_display_1_y5, n4_bits_7_seg_display_1_y6, n4_bits_7_seg_display_1_y7,
       n4_bits_7_seg_display_2_y0, n4_bits_7_seg_display_2_y1, n4_bits_7_seg_display_2_y2,
       n4_bits_7_seg_display_2_y3, n4_bits_7_seg_display_2_y4, n4_bits_7_seg_display_2_y5,
       n4_bits_7_seg_display_2_y6, n4_bits_7_seg_display_2_y7, n4_bits_7_seg_display_3_y0,
       n4_bits_7_seg_display_3_y1, n4_bits_7_seg_display_3_y2, n4_bits_7_seg_display_3_y3,
       n4_bits_7_seg_display_3_y4, n4_bits_7_seg_display_3_y5, n4_bits_7_seg_display_3_y6,
       n4_bits_7_seg_display_3_y7;
  wire [3:0] full_adder4_1_c;

  _4_bits_7_seg_display u_4_bits_7_seg_display_1 (
    .In3(in_1[3]), .In2(in_1[2]), .In1(in_1[1]), .In0(in_1[0]), .Y0(n4_bits_7_seg_display_1_y0),
    .Y1(n4_bits_7_seg_display_1_y1), .Y2(n4_bits_7_seg_display_1_y2), .Y3(n4_bits_7_seg_display_1_y3),
    .Y4(n4_bits_7_seg_display_1_y4), .Y5(n4_bits_7_seg_display_1_y5), .Y6(n4_bits_7_seg_display_1_y6),
    .Y7(n4_bits_7_seg_display_1_y7));
  Full_adder4 full_adder4_1 (
    .A(in_1), .B(in_2), .Cout(full_adder4_1_cout), .C(full_adder4_1_c), .Cin(1'b0));  // open: Overflow
  _4_bits_7_seg_display u_4_bits_7_seg_display_2 (
    .In3(in_2[3]), .In2(in_2[2]), .In1(in_2[1]), .In0(in_2[0]), .Y0(n4_bits_7_seg_display_2_y0),
    .Y1(n4_bits_7_seg_display_2_y1), .Y2(n4_bits_7_seg_display_2_y2), .Y3(n4_bits_7_seg_display_2_y3),
    .Y4(n4_bits_7_seg_display_2_y4), .Y5(n4_bits_7_seg_display_2_y5), .Y6(n4_bits_7_seg_display_2_y6),
    .Y7(n4_bits_7_seg_display_2_y7));
  _7_Segment_Display u_7_segment_display_1 (
    .g(n4_bits_7_seg_display_1_y0), .f(n4_bits_7_seg_display_1_y1), .a(n4_bits_7_seg_display_1_y2),
    .b(n4_bits_7_seg_display_1_y3), .e(n4_bits_7_seg_display_1_y4), .d(n4_bits_7_seg_display_1_y5),
    .c(n4_bits_7_seg_display_1_y6), .dp(n4_bits_7_seg_display_1_y7));
  _7_Segment_Display u_7_segment_display_2 (
    .g(n4_bits_7_seg_display_2_y0), .f(n4_bits_7_seg_display_2_y1), .a(n4_bits_7_seg_display_2_y2),
    .b(n4_bits_7_seg_display_2_y3), .e(n4_bits_7_seg_display_2_y4), .d(n4_bits_7_seg_display_2_y5),
    .c(n4_bits_7_seg_display_2_y6), .dp(n4_bits_7_seg_display_2_y7));
  LED led_1 (.in(full_adder4_1_cout));
  _4_bits_7_seg_display u_4_bits_7_seg_display_3 (
    .In3(full_adder4_1_c[3]), .In2(full_adder4_1_c[2]), .In1(full_adder4_1_c[1]), .In0(full_adder4_1_c[0]),
    .Y0(n4_bits_7_seg_display_3_y0), .Y1(n4_bits_7_seg_display_3_y1), .Y2(n4_bits_7_seg_display_3_y2),
    .Y3(n4_bits_7_seg_display_3_y3), .Y4(n4_bits_7_seg_display_3_y4), .Y5(n4_bits_7_seg_display_3_y5),
    .Y6(n4_bits_7_seg_display_3_y6), .Y7(n4_bits_7_seg_display_3_y7));
  _7_Segment_Display u_7_segment_display_3 (
    .g(n4_bits_7_seg_display_3_y0), .f(n4_bits_7_seg_display_3_y1), .a(n4_bits_7_seg_display_3_y2),
    .b(n4_bits_7_seg_display_3_y3), .e(n4_bits_7_seg_display_3_y4), .d(n4_bits_7_seg_display_3_y5),
    .c(n4_bits_7_seg_display_3_y6), .dp(n4_bits_7_seg_display_3_y7));
endmodule

module Full_adder4 (
  input  [3:0] A,
  input  Cin,
  input  [3:0] B,
  output Overflow,
  output Cout,
  output [3:0] C
);

  wire main_1_cout, main_2_cout, main_3_cout;

  Full_adder1_main main_1 (.Cin(Cin), .A(A[0]), .B(B[0]), .Cout(main_1_cout), .S(C[0]));
  Full_adder1_main main_2 (.Cin(main_1_cout), .A(A[1]), .B(B[1]), .Cout(main_2_cout), .S(C[1]));
  Full_adder1_main main_3 (.Cin(main_2_cout), .A(A[2]), .B(B[2]), .Cout(main_3_cout), .S(C[2]));
  Full_adder1_main main_4 (.Cin(main_3_cout), .A(A[3]), .B(B[3]), .Cout(Cout), .S(C[3]));
  xor xor_1 (Overflow, main_3_cout, Cout);
endmodule

module Full_subtractor4 (
  input  [3:0] A,
  input  [3:0] B,
  output out_3,
  output [3:0] C
);

  wire full_adder4_1_overflow;
  wire [3:0] xor_1_out;

  assign xor_1_out = B ^ 4'b1111;  // XOR_Gate xor_1, 4 bits wide
  Full_adder4 full_adder4_1 (.A(A), .B(xor_1_out), .Cout(out_3), .C(C), .Cin(1'b1), .Overflow(full_adder4_1_overflow));
  LED led_1 (.in(full_adder4_1_overflow));
endmodule

module Full_adder4_subtractor4 (
  input  [3:0] A,
  input  [3:0] B,
  input  op,
  output out_4,
  output [3:0] C
);

  wire full_adder4_1_overflow;
  wire [3:0] bit_extender_1_out, xor_1_out;

  assign bit_extender_1_out = {{3{op}}, op};  // Bit_Extender bit_extender_1
  assign xor_1_out = B ^ bit_extender_1_out;  // XOR_Gate xor_1, 4 bits wide
  Full_adder4 full_adder4_1 (.A(A), .B(xor_1_out), .Cout(out_4), .C(C), .Cin(op), .Overflow(full_adder4_1_overflow));
  LED led_1 (.in(full_adder4_1_overflow));
endmodule
