// Logisim project DFF.circ as structural Verilog: 6 circuits, main circuit main
module main (
  input  Rst,
  input  D,
  output Q
);

  wire button_1_out;

  Button button_1 (.out(button_1_out));
  DFF_rst dff_rst_1 (.Rst(Rst), .D(D), .clk(button_1_out), .Q(Q));
endmodule

module DFF (
  input  D,
  input  clk,
  output Q
);

  wire d_latch_1_q, not_1_out;

  not not_1 (not_1_out, clk);
  D_latch d_latch_1 (.WE(not_1_out), .D(D), .Q(d_latch_1_q));  // open: Q_bar
  D_latch d_latch_2 (.WE(clk), .D(d_latch_1_q), .Q(Q));  // open: Q_bar
endmodule

module DFF_rst (
  input  Rst,
  input  D,
  input  clk,
  output Q
);

  wire and_1_out, d_latch_1_q, not_1_out, not_2_out, or_1_out;

  not not_1 (not_1_out, clk);
  D_latch d_latch_1 (.WE(not_1_out), .D(D), .Q(d_latch_1_q));  // open: Q_bar
  not not_2 (not_2_out, Rst);
  and and_1 (and_1_out, not_2_out, d_latch_1_q);
  or or_1 (or_1_out, Rst, clk);
  D_latch d_latch_2 (.WE(or_1_out), .D(and_1_out), .Q(Q));  // open: Q_bar
endmodule

module TFF (
  input  Rst,
  input  En,
  input  T,
  input  clk,
  output Q
);

  wire and_1_out, xor_1_out;

  and and_1 (and_1_out, En, T);
  xor xor_1 (xor_1_out, Q, and_1_out);
  DFF_rst dff_rst_1 (.Rst(Rst), .D(xor_1_out), .clk(clk), .Q(Q));
endmodule

module DFF_neg (
  input  D,
  input  clk,
  output out_3
);

  wire d_latch_1_q, not_1_out;

  D_latch d_latch_1 (.WE(clk), .D(D), .Q(d_latch_1_q));  // open: Q_bar
  not not_1 (not_1_out, clk);
  D_latch d_latch_2 (.WE(not_1_out), .D(d_latch_1_q), .Q(out_3));  // open: Q_bar
endmodule

module DFF_rst_en (
  input  Rst,
  input  En,
  input  D,
  input  clk,
  output Q,
  output Q_bar
);

  wire and_1_out, and_2_out, d_latch_1_q, not_1_out, not_2_out, or_1_out;

  not not_1 (not_1_out, clk);
  and and_1 (and_1_out, En, not_1_out);
  D_latch d_latch_1 (.WE(and_1_out), .D(D), .Q(d_latch_1_q));  // open: Q_bar
  not not_2 (not_2_out, Rst);
  and and_2 (and_2_out, not_2_out, d_latch_1_q);
  or or_1 (or_1_out, Rst, clk);
  D_latch d_latch_2 (.WE(or_1_out), .D(and_2_out), .Q(Q), .Q_bar(Q_bar));
endmodule
