// Logisim project D_latch.circ as structural Verilog: 3 circuits, main circuit main
module main (
  input  Rst,
  output Q
);

  wire d_latch_rst_1_q_bar;

  D_latch_rst d_latch_rst_1 (.Rst(Rst), .D(d_latch_rst_1_q_bar), .Q(Q), .Q_bar(d_latch_rst_1_q_bar));
endmodule

module D_latch (
  input  WE,
  input  D,
  output Q,
  output Q_bar
);

  wire and_1_out, and_2_out, not_1_out;

  not not_1 (not_1_out, D);
  and and_1 (and_1_out, not_1_out, WE);
  and and_2 (and_2_out, WE, D);
  SR_latch_nor sr_latch_nor_1 (.R(and_1_out), .S(and_2_out), .Q(Q), .Q_bar(Q_bar));
endmodule

module D_latch_rst (
  input  Rst,
  input  D,
  output Q,
  output Q_bar
);

  wire and_1_out, not_1_out;

  not not_1 (not_1_out, Rst);
  and and_1 (and_1_out, not_1_out, D);
  D_latch d_latch_1 (.WE(1'b1), .D(and_1_out), .Q(Q), .Q_bar(Q_bar));
endmodule
