// Logisim project Reg4.circ as structural Verilog: 3 circuits, main circuit main
module main (
  input  En,
  input  [3:0] D
);

  wire clk_out, n4_bits_7_seg_display_1_y0, n4_bits_7_seg_display_1_y1, n4_bits_7_seg_display_1_y2,
       n4_bits_7_seg_display_1_y3, n4_bits_7_seg_display_1_y4, n4_bits_7_seg_display_1_y5,
       n4_bits_7_seg_display_1_y6, n4_bits_7_seg_display_1_y7;
  wire [3:0] reg4_1_q;

  Button clk (.out(clk_out));
  Reg4 reg4_1 (.En(En), .D(D), .clk(clk_out), .Q(reg4_1_q), .Rst(1'b0));
  _4_bits_7_seg_display u_4_bits_7_seg_display_1 (
    .In3(reg4_1_q[3]), .In2(reg4_1_q[2]), .In1(reg4_1_q[1]), .In0(reg4_1_q[0]),
    .Y0(n4_bits_7_seg_display_1_y0), .Y1(n4_bits_7_seg_display_1_y1), .Y2(n4_bits_7_seg_display_1_y2),
    .Y3(n4_bits_7_seg_display_1_y3), .Y4(n4_bits_7_seg_display_1_y4), .Y5(n4_bits_7_seg_display_1_y5),
    .Y6(n4_bits_7_seg_display_1_y6), .Y7(n4_bits_7_seg_display_1_y7));
  _7_Segment_Display u_7_segment_display_1 (
    .g(n4_bits_7_seg_display_1_y0), .f(n4_bits_7_seg_display_1_y1), .a(n4_bits_7_seg_display_1_y2),
    .b(n4_bits_7_seg_display_1_y3), .e(n4_bits_7_seg_display_1_y4), .d(n4_bits_7_seg_display_1_y5),
    .c(n4_bits_7_seg_display_1_y6), .dp(n4_bits_7_seg_display_1_y7));
endmodule

module Reg4 (
  input  Rst,
  input  En,
  input  [3:0] D,
  input  clk,
  output [3:0] Q
);

  DFF_rst_en dff_rst_en_1 (.Rst(Rst), .Q(Q[3]), .D(D[3]), .clk(clk), .En(En));  // open: Q_bar
  DFF_rst_en dff_rst_en_2 (.Rst(Rst), .Q(Q[2]), .D(D[2]), .clk(clk), .En(En));  // open: Q_bar
  DFF_rst_en dff_rst_en_3 (.Rst(Rst), .Q(Q[1]), .D(D[1]), .clk(clk), .En(En));  // open: Q_bar
  DFF_rst_en dff_rst_en_4 (.Rst(Rst), .Q(Q[0]), .D(D[0]), .clk(clk), .En(En));  // open: Q_bar
endmodule

module Counter4 (
  input  Rst,
  input  En,
  input  clk,
  output [3:0] Cnt
);

  wire [3:0] reg4_1_q;

  Reg4 reg4_1 (.En(En), .D(Cnt), .clk(clk), .Q(reg4_1_q), .Rst(Rst));
  Full_adder4 full_adder4_1 (.A(reg4_1_q), .B(4'b0001), .C(Cnt), .Cin(1'b0));  // open: Cout, Overflow
endmodule
