// Logisim project SR_latch.circ as structural Verilog: 3 circuits, main circuit main
module main (
  input  R,
  input  S,
  input  En,
  output Q,
  output Q_bar
);

  wire and_1_out, and_2_out;

  and and_1 (and_1_out, R, En);
  and and_2 (and_2_out, S, En);
  SR_latch_nor sr_latch_nor_1 (.R(and_1_out), .S(and_2_out), .Q(Q), .Q_bar(Q_bar));
endmodule

module SR_latch_nand (
  input  R,
  input  S,
  output Q,
  output Q_bar
);

  nand nand_1 (Q_bar, Q, S);
  nand nand_2 (Q, R, Q_bar);
endmodule

module SR_latch_nor (
  input  R,
  input  S,
  output Q,
  output Q_bar
);

  nor nor_1 (Q_bar, Q, S);
  nor nor_2 (Q, R, Q_bar);
endmodule
