// Logisim project Serial_sum.circ as structural Verilog: 4 circuits, main circuit main
module main (
  input  Rst,
  input  En,
  output [7:0] Sum
);

  wire clock_1_out, n4_bits_7_seg_display_1_y0, n4_bits_7_seg_display_1_y1, n4_bits_7_seg_display_1_y2,
       n4_bits_7_seg_display_1_y3, n4_bits_7_seg_display_1_y4, n4_bits_7_seg_display_1_y5,
       n4_bits_7_seg_display_1_y6, n4_bits_7_seg_display_1_y7, n4_bits_7_seg_display_2_y0,
       n4_bits_7_seg_display_2_y1, n4_bits_7_seg_display_2_y2, n4_bits_7_seg_display_2_y3,
       n4_bits_7_seg_display_2_y4, n4_bits_7_seg_display_2_y5, n4_bits_7_seg_display_2_y6,
       n4_bits_7_seg_display_2_y7;
  wire [7:0] counter8_1_out_4, reg8_1_q;

  Clock clock_1 (.out(clock_1_out));
  Counter8 counter8_1 (.Rst(Rst), .En(En), .clk(clock_1_out), .out_4(counter8_1_out_4));
  Reg8 reg8_1 (.Rst(Rst), .En(En), .D(Sum), .clk(clock_1_out), .Q(reg8_1_q));
  // Probe on counter8_1_out_4
  Full_adder8 full_adder8_1 (.A(counter8_1_out_4), .Cin(1'b0), .B(reg8_1_q), .out_5(Sum));  // open: Cout
  _4_bits_7_seg_display u_4_bits_7_seg_display_1 (
    .In3(Sum[7]), .In2(Sum[6]), .In1(Sum[5]), .In0(Sum[4]), .Y0(n4_bits_7_seg_display_1_y0),
    .Y1(n4_bits_7_seg_display_1_y1), .Y2(n4_bits_7_seg_display_1_y2), .Y3(n4_bits_7_seg_display_1_y3),
    .Y4(n4_bits_7_seg_display_1_y4), .Y5(n4_bits_7_seg_display_1_y5), .Y6(n4_bits_7_seg_display_1_y6),
    .Y7(n4_bits_7_seg_display_1_y7));
  _4_bits_7_seg_display u_4_bits_7_seg_display_2 (
    .In3(Sum[3]), .In2(Sum[2]), .In1(Sum[1]), .In0(Sum[0]), .Y0(n4_bits_7_seg_display_2_y0),
    .Y1(n4_bits_7_seg_display_2_y1), .Y2(n4_bits_7_seg_display_2_y2), .Y3(n4_bits_7_seg_display_2_y3),
    .Y4(n4_bits_7_seg_display_2_y4), .Y5(n4_bits_7_seg_display_2_y5), .Y6(n4_bits_7_seg_display_2_y6),
    .Y7(n4_bits_7_seg_display_2_y7));
  _7_Segment_Display u_7_segment_display_1 (
    .g(n4_bits_7_seg_display_1_y0), .f(n4_bits_7_seg_display_1_y1), .a(n4_bits_7_seg_display_1_y2),
    .b(n4_bits_7_seg_display_1_y3), .e(n4_bits_7_seg_display_1_y4), .d(n4_bits_7_seg_display_1_y5),
    .c(n4_bits_7_seg_display_1_y6), .dp(n4_bits_7_seg_display_1_y7));
  _7_Segment_Display u_7_segment_display_2 (
    .g(n4_bits_7_seg_display_2_y0), .f(n4_bits_7_seg_display_2_y1), .a(n4_bits_7_seg_display_2_y2),
    .b(n4_bits_7_seg_display_2_y3), .e(n4_bits_7_seg_display_2_y4), .d(n4_bits_7_seg_display_2_y5),
    .c(n4_bits_7_seg_display_2_y6), .dp(n4_bits_7_seg_display_2_y7));
endmodule

module Full_adder8 (
  input  [7:0] A,
  input  [7:0] B,
  input  Cin,
  output Cout,
  output [7:0] out_5
);

  wire full_adder4_1_cout;

  Full_adder4 full_adder4_1 (
    .A(A[3:0]), .B(B[3:0]), .Cout(full_adder4_1_cout), .C(out_5[3:0]), .Cin(Cin));  // open: Overflow
  Full_adder4 full_adder4_2 (
    .A(A[7:4]), .B(B[7:4]), .Cout(Cout), .C(out_5[7:4]), .Cin(full_adder4_1_cout));  // open: Overflow

  // Notes on the sheet:
  //   C
endmodule

module Reg8 (
  input  Rst,
  input  En,
  input  [7:0] D,
  input  clk,
  output [7:0] Q
);

  Reg4 reg4_1 (.En(En), .D(D[3:0]), .clk(clk), .Q(Q[3:0]), .Rst(Rst));
  Reg4 reg4_2 (.En(En), .D(D[7:4]), .clk(clk), .Q(Q[7:4]), .Rst(Rst));
endmodule

module Counter8 (
  input  Rst,
  input  En,
  input  clk,
  output [7:0] out_4
);

  wire [7:0] reg8_1_q;

  Reg8 reg8_1 (.Rst(Rst), .En(En), .D(out_4), .clk(clk), .Q(reg8_1_q));
  Full_adder8 full_adder8_1 (.A(8'h1), .Cin(1'b0), .B(reg8_1_q), .out_5(out_4));  // open: Cout
endmodule
