// Logisim project Simple_RV32I_CPU.circ as structural Verilog: 10 circuits, main circuit PC_reg
module PC_reg (
  input  [31:0] PCNext,
  input  CLK,
  input  RST,
  output [31:0] PC
);

  Register #(.width(32)) register_1 (.D(PCNext), .en(1'b1), .clk(CLK), .Q(PC), .clr(RST));
endmodule

module Instr_Mem (
  input  [31:0] Addr,
  output [31:0] Instr
);

  wire [15:0] bit_extender_1_out;

  Bit_Extender #(.in_width(32), .\type ("zero")) bit_extender_1 (.in(Addr), .out(bit_extender_1_out));
  ROM #(.addrWidth(16), .dataWidth(32)) rom_1 (.addr(bit_extender_1_out), .data(Instr));
endmodule

module Regfile (
  input  CLK,
  input  [31:0] WData,
  input  [4:0] WAddr,
  input  WE,
  input  RST,
  input  [4:0] RAddr1,
  input  [4:0] RAddr2,
  output [31:0] RData1,
  output [31:0] RData2
);

  wire decoder_1_out0, decoder_1_out1, decoder_1_out2, decoder_1_out3, decoder_1_out4, decoder_1_out5,
       decoder_1_out6, decoder_1_out7, decoder_1_out8, decoder_1_out9, decoder_1_out10, decoder_1_out11,
       decoder_1_out12, decoder_1_out13, decoder_1_out14, decoder_1_out15;
  wire [3:0] bit_extender_1_out, bit_extender_2_out, bit_extender_3_out;
  wire [31:0] register_1_q, register_2_q, register_3_q, register_4_q, register_5_q, register_6_q,
       register_7_q, register_8_q, register_9_q, register_10_q, register_11_q, register_12_q, register_13_q,
       register_14_q, register_15_q, register_16_q;

  Bit_Extender #(.in_width(5), .out_width(4), .\type ("zero")) bit_extender_1 (.in(WAddr), .out(bit_extender_1_out));
  Decoder #(.select(4)) decoder_1 (
    .out0(decoder_1_out0), .out1(decoder_1_out1), .out2(decoder_1_out2), .out3(decoder_1_out3),
    .out4(decoder_1_out4), .out5(decoder_1_out5), .out6(decoder_1_out6), .out7(decoder_1_out7),
    .out8(decoder_1_out8), .out9(decoder_1_out9), .out10(decoder_1_out10), .out11(decoder_1_out11),
    .out12(decoder_1_out12), .out13(decoder_1_out13), .out14(decoder_1_out14), .out15(decoder_1_out15),
    .sel(bit_extender_1_out), .en(WE));
  Bit_Extender #(.in_width(5), .out_width(4), .\type ("zero")) bit_extender_2 (.in(RAddr1), .out(bit_extender_2_out));
  Bit_Extender #(.in_width(5), .out_width(4), .\type ("zero")) bit_extender_3 (.in(RAddr2), .out(bit_extender_3_out));
  Register #(.width(32)) register_1 (.D({32{1'b0}}), .en(decoder_1_out0), .clk(CLK), .Q(register_1_q), .clr(RST));
  Register #(.width(32)) register_2 (.D(WData), .en(decoder_1_out8), .clk(CLK), .Q(register_2_q), .clr(RST));
  Register #(.width(32)) register_3 (.D(WData), .en(decoder_1_out1), .clk(CLK), .Q(register_3_q), .clr(RST));
  Register #(.width(32)) register_4 (.D(WData), .en(decoder_1_out9), .clk(CLK), .Q(register_4_q), .clr(RST));
  Register #(.width(32)) register_5 (.D(WData), .en(decoder_1_out2), .clk(CLK), .Q(register_5_q), .clr(RST));
  Register #(.width(32)) register_6 (.D(WData), .en(decoder_1_out10), .clk(CLK), .Q(register_6_q), .clr(RST));
  Register #(.width(32)) register_7 (.D(WData), .en(decoder_1_out3), .clk(CLK), .Q(register_7_q), .clr(RST));
  Register #(.width(32)) register_8 (.D(WData), .en(decoder_1_out11), .clk(CLK), .Q(register_8_q), .clr(RST));
  Register #(.width(32)) register_9 (.D(WData), .en(decoder_1_out4), .clk(CLK), .Q(register_9_q), .clr(RST));
  Register #(.width(32)) register_10 (.D(WData), .en(decoder_1_out12), .clk(CLK), .Q(register_10_q), .clr(RST));
  Register #(.width(32)) register_11 (.D(WData), .en(decoder_1_out5), .clk(CLK), .Q(register_11_q), .clr(RST));
  Register #(.width(32)) register_12 (.D(WData), .en(decoder_1_out13), .clk(CLK), .Q(register_12_q), .clr(RST));
  Register #(.width(32)) register_13 (.D(WData), .en(decoder_1_out6), .clk(CLK), .Q(register_13_q), .clr(RST));
  Register #(.width(32)) register_14 (.D(WData), .en(decoder_1_out14), .clk(CLK), .Q(register_14_q), .clr(RST));
  Register #(.width(32)) register_15 (.D(WData), .en(decoder_1_out7), .clk(CLK), .Q(register_15_q), .clr(RST));
  Register #(.width(32)) register_16 (.D(WData), .en(decoder_1_out15), .clk(CLK), .Q(register_16_q), .clr(RST));
  Multiplexer #(.select(4), .width(32)) multiplexer_1 (
    .in0(register_1_q), .in1(register_3_q), .in2(register_5_q), .in3(register_7_q), .in4(register_9_q),
    .in5(register_11_q), .in6(register_13_q), .in7(register_15_q), .in8(register_2_q), .in9(register_4_q),
    .in10(register_6_q), .in11(register_8_q), .in12(register_10_q), .in13(register_12_q),
    .in14(register_14_q), .in15(register_16_q), .out(RData1), .sel(bit_extender_2_out));
  Multiplexer #(.select(4), .width(32)) multiplexer_2 (
    .in0(register_1_q), .in1(register_3_q), .in2(register_5_q), .in3(register_7_q), .in4(register_9_q),
    .in5(register_11_q), .in6(register_13_q), .in7(register_15_q), .in8(register_2_q), .in9(register_4_q),
    .in10(register_6_q), .in11(register_8_q), .in12(register_10_q), .in13(register_12_q),
    .in14(register_14_q), .in15(register_16_q), .out(RData2), .sel(bit_extender_3_out));
endmodule

module datapath_single_cycle (
  input  RST
);

  wire alu_1_zero, CLK_out, controller_1_alusrc, controller_1_memwrite, controller_1_pcsrc,
       controller_1_regwrite, controller_1_resultsrc;
  wire [1:0] controller_1_immsrc;
  wire [2:0] controller_1_alucontrol;
  wire [31:0] adder_1_out, adder_2_out, alu_1_result, data_mem_1_rdata, extend_1_imm32, instr_mem_1_instr,
       multiplexer_1_out, multiplexer_2_out, multiplexer_3_out, pc_reg_1_pc, regfile_1_rdata1,
       regfile_1_rdata2;

  Button CLK (.out(CLK_out));
  Multiplexer #(.width(32)) multiplexer_1 (
    .in0(adder_1_out), .in1(adder_2_out), .out(multiplexer_1_out), .sel(controller_1_pcsrc));
  PC_reg pc_reg_1 (.PCNext(multiplexer_1_out), .CLK(CLK_out), .RST(RST), .PC(pc_reg_1_pc));
  Adder #(.width(32)) adder_1 (.a(pc_reg_1_pc), .b(32'h4), .out(adder_1_out));  // open: cin, cout
  Instr_Mem instr_mem_1 (.Addr(pc_reg_1_pc), .Instr(instr_mem_1_instr));
  Controller controller_1 (
    .zero(alu_1_zero), .op(instr_mem_1_instr[6:0]), .funct3(instr_mem_1_instr[14:12]),
    .funct7_5(instr_mem_1_instr[30]), .PCSrc(controller_1_pcsrc), .RegWrite(controller_1_regwrite),
    .ImmSrc(controller_1_immsrc), .ALUSrc(controller_1_alusrc), .MemWrite(controller_1_memwrite),
    .ResultSrc(controller_1_resultsrc), .ALUControl(controller_1_alucontrol));
  Regfile regfile_1 (
    .CLK(CLK_out), .WData(multiplexer_3_out), .WAddr(instr_mem_1_instr[11:7]), .WE(controller_1_regwrite),
    .RST(RST), .RAddr1(instr_mem_1_instr[19:15]), .RAddr2(instr_mem_1_instr[24:20]),
    .RData1(regfile_1_rdata1), .RData2(regfile_1_rdata2));
  Extend extend_1 (.ImmSrc(controller_1_immsrc), .Imm(instr_mem_1_instr[31:7]), .Imm32(extend_1_imm32));
  Multiplexer #(.width(32)) multiplexer_2 (
    .in0(regfile_1_rdata2), .in1(extend_1_imm32), .out(multiplexer_2_out), .sel(controller_1_alusrc));
  Adder #(.width(32)) adder_2 (.a(pc_reg_1_pc), .b(extend_1_imm32), .out(adder_2_out));  // open: cin, cout
  ALU alu_1 (
    .A(regfile_1_rdata1), .B(multiplexer_2_out), .ALUControl(controller_1_alucontrol), .Result(alu_1_result),
    .Zero(alu_1_zero));  // open: Negative, Carry, Overflow
  Data_Mem data_mem_1 (
    .Addr(alu_1_result), .WE(controller_1_memwrite), .CLK(CLK_out), .WData(regfile_1_rdata2),
    .RData(data_mem_1_rdata));
  Multiplexer #(.width(32)) multiplexer_3 (
    .in0(alu_1_result), .in1(data_mem_1_rdata), .out(multiplexer_3_out), .sel(controller_1_resultsrc));
endmodule

module Data_Mem (
  input  [31:0] Addr,
  input  WE,
  input  CLK,
  input  [31:0] WData,
  output [31:0] RData
);

  wire [15:0] bit_extender_1_out;

  Bit_Extender #(.in_width(32), .\type ("zero")) bit_extender_1 (.in(Addr), .out(bit_extender_1_out));
  RAM #(.addrWidth(16), .dataWidth(32)) ram_1 (
    .addr(bit_extender_1_out), .we(WE), .oe(1'b1), .clk(CLK), .din(WData), .dout(RData));
endmodule

module Extend (
  input  [1:0] ImmSrc,
  input  [24:0] Imm,
  output [31:0] Imm32
);

  wire [19:0] bit_extender_1_out;

  assign bit_extender_1_out = {{19{Imm[24]}}, Imm[24]};  // Bit_Extender bit_extender_1
  Multiplexer #(.select(2), .width(32)) multiplexer_1 (
    .in0({bit_extender_1_out, Imm[24:13]}), .in1({bit_extender_1_out, Imm[24:18], Imm[4:0]}),
    .in2({bit_extender_1_out, Imm[0], Imm[23:18], Imm[4:1], 1'b0}), .out(Imm32), .sel(ImmSrc));  // open: in3
endmodule

module ALU (
  input  [31:0] A,
  input  [31:0] B,
  input  [2:0] ALUControl,
  output [31:0] Result,
  output Zero,
  output Negative,
  output Carry,
  output Overflow
);

  wire adder_1_cout, not_2_out, xnor_1_out, xor_1_out, xor_2_out;
  wire [31:0] adder_1_out, and_1_out, bit_extender_1_out, multiplexer_1_out, not_1_out, or_1_out;

  assign not_1_out = ~B;  // NOT_Gate not_1, 32 bits wide
  Multiplexer #(.width(32)) multiplexer_1 (.in0(B), .in1(not_1_out), .out(multiplexer_1_out), .sel(ALUControl[0]));
  not not_2 (not_2_out, ALUControl[1]);
  assign or_1_out = A | B;  // OR_Gate or_1, 32 bits wide
  assign and_1_out = A & B;  // AND_Gate and_1, 32 bits wide
  Adder #(.width(32)) adder_1 (
    .a(A), .b(multiplexer_1_out), .out(adder_1_out), .cin(ALUControl[0]), .cout(adder_1_cout));
  xor xor_1 (xor_1_out, A[31], adder_1_out[31]);
  NotExactlyOne xnor_1 (.out(xnor_1_out), .in0(A[31]), .in1(B[31]), .in2(ALUControl[0]));
  and and_2 (Overflow, not_2_out, xor_1_out, xnor_1_out);
  xor xor_2 (xor_2_out, Overflow, adder_1_out[31]);
  assign bit_extender_1_out = {{31{1'b0}}, xor_2_out};  // Bit_Extender bit_extender_1
  Multiplexer #(.select(3), .width(32)) multiplexer_2 (
    .in0(adder_1_out), .in1(adder_1_out), .in2(and_1_out), .in3(or_1_out), .in5(bit_extender_1_out),
    .out({Negative, Result[30:0]}), .sel(ALUControl));  // open: in4, in6, in7
  Comparator #(.width(32)) comparator_1 (.a({Negative, Result[30:0]}), .b({32{1'b0}}), .eq(Zero));  // open: gt, lt
  and and_3 (Carry, adder_1_cout, not_2_out);

  assign Result[31] = Negative;
endmodule

module Controller (
  input  zero,
  input  [6:0] op,
  input  [2:0] funct3,
  input  funct7_5,
  output PCSrc,
  output RegWrite,
  output [1:0] ImmSrc,
  output ALUSrc,
  output MemWrite,
  output ResultSrc,
  output [2:0] ALUControl
);

  wire main_decoder_1_branch;
  wire [1:0] main_decoder_1_aluop;

  Main_Decoder main_decoder_1 (
    .op(op), .RegWrite(RegWrite), .ImmSrc(ImmSrc), .ALUSrc(ALUSrc), .MemWrite(MemWrite),
    .ResultSrc(ResultSrc), .Branch(main_decoder_1_branch), .ALUOp(main_decoder_1_aluop));
  and and_1 (PCSrc, zero, main_decoder_1_branch);
  ALU_Decoder alu_decoder_1 (
    .ALUOp(main_decoder_1_aluop), .funct3(funct3), .op5(op[5]), .funct7_5(funct7_5), .ALUControl(ALUControl));
endmodule

module Main_Decoder (
  input  [6:0] op,
  output RegWrite,
  output [1:0] ImmSrc,
  output ALUSrc,
  output MemWrite,
  output ResultSrc,
  output Branch,
  output [1:0] ALUOp
);

  wire comparator_1_eq, decoder_1_out1, decoder_1_out3;

  Comparator #(.width(4)) comparator_1 (.a(4'b0011), .b(op[3:0]), .eq(comparator_1_eq));  // open: gt, lt
  Decoder #(.select(3)) decoder_1 (
    .out0(ResultSrc), .out1(decoder_1_out1), .out2(ImmSrc[0]), .out3(decoder_1_out3), .out6(ALUOp[0]),
    .sel(op[6:4]), .en(comparator_1_eq));  // open: out4, out5, out7
  or or_1 (RegWrite, ResultSrc, decoder_1_out1, decoder_1_out3);
  or or_2 (ALUSrc, ResultSrc, decoder_1_out1, ImmSrc[0]);
  and and_1 (ALUOp[1], decoder_1_out3, decoder_1_out1);

  assign Branch = ALUOp[0];
  assign ImmSrc[1] = ALUOp[0];
  assign MemWrite = ImmSrc[0];
endmodule

module ALU_Decoder (
  input  [1:0] ALUOp,
  input  [2:0] funct3,
  input  op5,
  input  funct7_5,
  output [2:0] ALUControl
);

  wire and_1_out, and_2_out, and_4_out, and_5_out, and_6_out, decoder_1_out1, decoder_1_out2, decoder_2_out0,
       decoder_2_out2, decoder_2_out6, decoder_2_out7, decoder_3_out3;

  Decoder #(.enable("false"), .select(2)) decoder_1 (
    .out1(decoder_1_out1), .out2(decoder_1_out2), .sel(ALUOp));  // open: out0, out3
  Decoder #(.enable("false"), .select(3)) decoder_2 (
    .out0(decoder_2_out0), .out2(decoder_2_out2), .out6(decoder_2_out6), .out7(decoder_2_out7), .sel(funct3));  // open: out1, out3, out4, out5
  Decoder #(.enable("false"), .select(2)) decoder_3 (
    .out3(decoder_3_out3), .sel({op5, funct7_5}));  // open: out0, out1, out2
  and and_1 (and_1_out, decoder_1_out2, decoder_2_out6);
  and and_2 (and_2_out, decoder_1_out2, decoder_2_out7);
  or or_1 (ALUControl[1], and_1_out, and_2_out);
  and and_3 (ALUControl[2], decoder_2_out2, decoder_1_out2);
  and and_4 (and_4_out, decoder_1_out2, decoder_2_out0, decoder_3_out3);
  and and_5 (and_5_out, decoder_1_out2, decoder_2_out2);
  and and_6 (and_6_out, decoder_1_out2, decoder_2_out6);
  or or_2 (ALUControl[0], decoder_1_out1, and_4_out, and_5_out, and_6_out);
endmodule
