// Logisim project Time_clock.circ as structural Verilog
module BCD_counter (
  input  Rst,
  input  En,
  input  clk,
  output Y,
  output [3:0] Cnt
);

  wire and_2_out, and_3_out, and_4_out, not_1_out, or_1_out;

  or or_1 (or_1_out, Y, and_2_out);
  and and_1 (Y, Cnt[0], Cnt[3]);
  and and_2 (and_2_out, Cnt[2], and_3_out);
  TFF tff_1 (.Rst(Rst), .clk(clk), .Q(Cnt[3]), .T(or_1_out), .En(En));
  and and_3 (and_3_out, Cnt[1], Cnt[0]);
  not not_1 (not_1_out, Cnt[3]);
  and and_4 (and_4_out, not_1_out, Cnt[0]);
  TFF tff_2 (.Rst(Rst), .clk(clk), .Q(Cnt[2]), .T(and_3_out), .En(En));
  TFF tff_3 (.Rst(Rst), .clk(clk), .Q(Cnt[1]), .T(and_4_out), .En(En));
  TFF tff_4 (.Rst(Rst), .clk(clk), .Q(Cnt[0]), .T(1'b1), .En(En));
endmodule

module Counter100 (
  input  Rst,
  input  Count_en,
  input  clk,
  output Y,
  output [3:0] One,
  output [3:0] Ten
);

  wire bcd_counter_1_y, bcd_counter_2_y;

  BCD_counter bcd_counter_1 (.Rst(Rst), .clk(clk), .Y(bcd_counter_1_y), .Cnt(Ten), .En(bcd_counter_2_y));
  and and_1 (Y, bcd_counter_1_y, bcd_counter_2_y);
  BCD_counter bcd_counter_2 (.Rst(Rst), .clk(clk), .Y(bcd_counter_2_y), .Cnt(One), .En(Count_en));

  // Notes on the sheet:
  //   Ten: pull=down
  //   One: pull=down
endmodule

module Counter60 (
  input  Rst,
  input  Count_en,
  output out_3
);

  wire and_1_out, and_2_out, and_3_out, bcd_counter_load_2_y, clock_1_out, n4_bits_7_seg_display_1_y0,
       n4_bits_7_seg_display_1_y1, n4_bits_7_seg_display_1_y2, n4_bits_7_seg_display_1_y3,
       n4_bits_7_seg_display_1_y4, n4_bits_7_seg_display_1_y5, n4_bits_7_seg_display_1_y6,
       n4_bits_7_seg_display_1_y7, n4_bits_7_seg_display_2_y0, n4_bits_7_seg_display_2_y1,
       n4_bits_7_seg_display_2_y2, n4_bits_7_seg_display_2_y3, n4_bits_7_seg_display_2_y4,
       n4_bits_7_seg_display_2_y5, n4_bits_7_seg_display_2_y6, n4_bits_7_seg_display_2_y7;
  wire [3:0] bcd_counter_load_1_data_out, bcd_counter_load_2_data_out;

  Clock clock_1 (.out(clock_1_out));
  BCD_counter_load bcd_counter_load_1 (
    .Rst(Rst), .En(bcd_counter_load_2_y), .clk(clock_1_out), .Load(and_3_out), .Data_in(4'b0000), .Y(out_3),
    .Data_out(bcd_counter_load_1_data_out));
  and and_1 (and_1_out, bcd_counter_load_1_data_out[0], bcd_counter_load_1_data_out[2]);
  BCD_counter_load bcd_counter_load_2 (
    .Rst(Rst), .En(Count_en), .clk(clock_1_out), .Load(1'b0), .Data_in(4'b0000), .Y(bcd_counter_load_2_y),
    .Data_out(bcd_counter_load_2_data_out));
  and and_2 (and_2_out, bcd_counter_load_2_data_out[0], bcd_counter_load_2_data_out[3]);
  and and_3 (and_3_out, and_1_out, and_2_out);
  LED led_1 (.in(and_3_out));
  _4_bits_7_seg_display u_4_bits_7_seg_display_1 (
    .In3(bcd_counter_load_1_data_out[3]), .In2(bcd_counter_load_1_data_out[2]),
    .In1(bcd_counter_load_1_data_out[1]), .In0(bcd_counter_load_1_data_out[0]),
    .Y0(n4_bits_7_seg_display_1_y0), .Y1(n4_bits_7_seg_display_1_y1), .Y2(n4_bits_7_seg_display_1_y2),
    .Y3(n4_bits_7_seg_display_1_y3), .Y4(n4_bits_7_seg_display_1_y4), .Y5(n4_bits_7_seg_display_1_y5),
    .Y6(n4_bits_7_seg_display_1_y6), .Y7(n4_bits_7_seg_display_1_y7));
  _4_bits_7_seg_display u_4_bits_7_seg_display_2 (
    .In3(bcd_counter_load_2_data_out[3]), .In2(bcd_counter_load_2_data_out[2]),
    .In1(bcd_counter_load_2_data_out[1]), .In0(bcd_counter_load_2_data_out[0]),
    .Y0(n4_bits_7_seg_display_2_y0), .Y1(n4_bits_7_seg_display_2_y1), .Y2(n4_bits_7_seg_display_2_y2),
    .Y3(n4_bits_7_seg_display_2_y3), .Y4(n4_bits_7_seg_display_2_y4), .Y5(n4_bits_7_seg_display_2_y5),
    .Y6(n4_bits_7_seg_display_2_y6), .Y7(n4_bits_7_seg_display_2_y7));
  _7_Segment_Display u_7_segment_display_1 (
    .g(n4_bits_7_seg_display_2_y0), .f(n4_bits_7_seg_display_2_y1), .a(n4_bits_7_seg_display_2_y2),
    .b(n4_bits_7_seg_display_2_y3), .e(n4_bits_7_seg_display_2_y4), .d(n4_bits_7_seg_display_2_y5),
    .c(n4_bits_7_seg_display_2_y6), .dp(n4_bits_7_seg_display_2_y7));
  _7_Segment_Display u_7_segment_display_2 (
    .g(n4_bits_7_seg_display_1_y0), .f(n4_bits_7_seg_display_1_y1), .a(n4_bits_7_seg_display_1_y2),
    .b(n4_bits_7_seg_display_1_y3), .e(n4_bits_7_seg_display_1_y4), .d(n4_bits_7_seg_display_1_y5),
    .c(n4_bits_7_seg_display_1_y6), .dp(n4_bits_7_seg_display_1_y7));
endmodule

module BCD_counter_load (
  input  Rst,
  input  En,
  input  clk,
  input  Load,
  input  [3:0] Data_in,
  output Y,
  output [3:0] Data_out
);

  wire and_1_out, and_2_out, and_3_out, and_4_out, and_5_out, and_6_out, and_7_out, dff_rst_en_1_q_bar,
       dff_rst_en_3_q_bar, dff_rst_en_4_q_bar, multiplexer_1_out, multiplexer_2_out, multiplexer_3_out,
       multiplexer_4_out, or_1_out, or_2_out, xor_1_out, xor_2_out;

  Multiplexer #(.enable("false")) multiplexer_1 (.in0(or_1_out), .in1(Data_in[3]), .out(multiplexer_1_out), .sel(Load));
  or or_1 (or_1_out, and_1_out, and_2_out);
  DFF_rst_en dff_rst_en_1 (
    .Rst(Rst), .Q(Data_out[3]), .D(multiplexer_1_out), .clk(clk), .En(En), .Q_bar(dff_rst_en_1_q_bar));
  and and_1 (and_1_out, Data_out[3], dff_rst_en_4_q_bar);
  or or_2 (or_2_out, and_3_out, and_4_out);
  and and_2 (and_2_out, Data_out[2], Data_out[1], Data_out[0]);
  Multiplexer #(.enable("false")) multiplexer_2 (.in0(or_2_out), .in1(Data_in[2]), .out(multiplexer_2_out), .sel(Load));
  xor xor_1 (xor_1_out, Data_out[0], Data_out[2]);
  and and_3 (and_3_out, xor_1_out, and_6_out);
  and and_4 (and_4_out, dff_rst_en_1_q_bar, and_5_out);
  and and_5 (and_5_out, dff_rst_en_3_q_bar, Data_out[2]);
  DFF_rst_en dff_rst_en_2 (.Rst(Rst), .Q(Data_out[2]), .D(multiplexer_2_out), .clk(clk), .En(En));  // open: Q_bar
  Multiplexer #(.enable("false")) multiplexer_3 (
    .in0(and_7_out), .in1(Data_in[1]), .out(multiplexer_3_out), .sel(Load));
  and and_6 (and_6_out, dff_rst_en_1_q_bar, Data_out[1]);
  and and_7 (and_7_out, dff_rst_en_1_q_bar, xor_2_out);
  xor xor_2 (xor_2_out, Data_out[0], Data_out[1]);
  DFF_rst_en dff_rst_en_3 (
    .Rst(Rst), .Q(Data_out[1]), .D(multiplexer_3_out), .clk(clk), .En(En), .Q_bar(dff_rst_en_3_q_bar));
  Multiplexer #(.enable("false")) multiplexer_4 (
    .in0(dff_rst_en_4_q_bar), .in1(Data_in[0]), .out(multiplexer_4_out), .sel(Load));
  DFF_rst_en dff_rst_en_4 (
    .Rst(Rst), .Q(Data_out[0]), .D(multiplexer_4_out), .clk(clk), .En(En), .Q_bar(dff_rst_en_4_q_bar));
  and and_8 (Y, Data_out[0], Data_out[3]);
endmodule
