// Logisim project Minirv.circ as structural Verilog: 11 circuits, main circuit minirv_datapath
module minirv_datapath (
  input  RST,
  output [15:0] ClockCycleCount
);

  wire addrdecoder_1_ismem, addrdecoder_1_isvga, and_2_out, button_1_out, control_unit_1_alusrc,
       control_unit_1_bytesrc, control_unit_1_memwrite, control_unit_1_pcsrc, control_unit_1_regwrite,
       rgb_video_1_p3;
  wire [1:0] control_unit_1_immsrc, control_unit_1_resultsrc;
  wire [3:0] multiplexer_3_out;
  wire [7:0] rgb_video_1_p4, rgb_video_1_p5;
  wire [23:0] rgb_video_1_p6;
  wire [31:0] adder_1_out, adder_2_out, byteselect_1_wordselected, immextend_1_imm32, mem_data_mem_1_rdata,
       mem_instr_mem_1_instr, multiplexer_1_out, multiplexer_2_out, multiplexer_4_out, pc_reg_1_pc,
       regfile_1_rdata1, regfile_1_rdata2;

  Button button_1 (.out(button_1_out));
  Clock CLK ();  // open: out
  Multiplexer #(.width(32)) multiplexer_1 (
    .in0(adder_1_out), .in1(adder_2_out), .out(multiplexer_1_out), .sel(control_unit_1_pcsrc));
  Counter #(.max('hffff), .width(16)) CycleCounter (
    .clr(RST), .load(1'b0), .up(1'b1), .count(1'b1), .clk(button_1_out), .Q(ClockCycleCount));  // open: D, carry
  // Probe on pc_reg_1_pc
  PC_reg pc_reg_1 (.PCNext(multiplexer_1_out), .CLK(button_1_out), .RST(RST), .PC(pc_reg_1_pc));
  Adder #(.width(32)) adder_1 (.a(pc_reg_1_pc), .b(32'h1), .out(adder_1_out));  // open: cin, cout
  // Probe on mem_instr_mem_1_instr
  mem_instr_Mem mem_instr_mem_1 (.Addr(pc_reg_1_pc), .Instr(mem_instr_mem_1_instr));
  Control_Unit control_unit_1 (
    .opcode(mem_instr_mem_1_instr[6:0]), .funct3(mem_instr_mem_1_instr[14:12]), .PCSrc(control_unit_1_pcsrc),
    .ImmSrc(control_unit_1_immsrc), .RegWrite(control_unit_1_regwrite), .ALUSrc(control_unit_1_alusrc),
    .MemWrite(control_unit_1_memwrite), .ResultSrc(control_unit_1_resultsrc), .ByteSrc(control_unit_1_bytesrc));
  // RGB_Video #(.cursor("No Cursor"), .height(256), .width(256)) rgb_video_1: pin names not known; wires that end beside it: RST, button_1_out, rgb_video_1_p3, rgb_video_1_p4, rgb_video_1_p5, rgb_video_1_p6
  Regfile regfile_1 (
    .CLK(button_1_out), .WData(multiplexer_4_out), .WAddr(mem_instr_mem_1_instr[11:7]),
    .WE(control_unit_1_regwrite), .RST(RST), .RAddr1(mem_instr_mem_1_instr[19:15]),
    .RAddr2(mem_instr_mem_1_instr[24:20]), .RData1(regfile_1_rdata1), .RData2(regfile_1_rdata2));
  ImmExtend immextend_1 (.ImmSrc(control_unit_1_immsrc), .Instr(mem_instr_mem_1_instr), .Imm32(immextend_1_imm32));
  Bit_Extender #(.in_width(32), .out_width(24)) bit_extender_1 (.in(regfile_1_rdata2), .out(rgb_video_1_p6));
  Multiplexer #(.width(32)) multiplexer_2 (
    .in0(regfile_1_rdata2), .in1(immextend_1_imm32), .out(multiplexer_2_out), .sel(control_unit_1_alusrc));
  Adder #(.width(32)) adder_2 (.a(regfile_1_rdata1), .b(multiplexer_2_out), .out(adder_2_out));  // open: cin, cout
  Multiplexer #(.width(4)) multiplexer_3 (
    .in0(4'b0001), .in1(4'b1111), .out(multiplexer_3_out), .sel(control_unit_1_bytesrc));
  Addr2Coordinates addr2coordinates_1 (.Addr(adder_2_out), .x_coor(rgb_video_1_p4), .y_coor(rgb_video_1_p5));
  and and_1 (rgb_video_1_p3, addrdecoder_1_isvga, control_unit_1_memwrite);
  AddrDecoder addrdecoder_1 (.Addr(adder_2_out), .isVGA(addrdecoder_1_isvga), .isMem(addrdecoder_1_ismem));
  and and_2 (and_2_out, addrdecoder_1_ismem, control_unit_1_memwrite);
  mem_data_Mem mem_data_mem_1 (
    .Addr(adder_2_out), .WE(and_2_out), .ByteEnable(multiplexer_3_out), .CLK(button_1_out),
    .WData(regfile_1_rdata2), .RData(mem_data_mem_1_rdata));
  ByteSelect byteselect_1 (
    .ByteSel(control_unit_1_bytesrc), .RWord(mem_data_mem_1_rdata), .WordSelected(byteselect_1_wordselected));
  Multiplexer #(.select(2), .width(32)) multiplexer_4 (
    .in0(adder_2_out), .in1(adder_1_out), .in2(byteselect_1_wordselected), .in3(immextend_1_imm32),
    .out(multiplexer_4_out));  // open: sel

  // Notes on the sheet:
  //   PCSrc
  //   RegWrite
  //   ALUSrc
  //   MemWrite
  //   ResultSrc
endmodule

module ImmExtend (
  input  [1:0] ImmSrc,
  input  [31:0] Instr,
  output [31:0] Imm32
);

  wire [20:0] bit_extender_1_out, bit_extender_2_out;

  assign bit_extender_1_out = {{20{Instr[31]}}, Instr[31]};  // Bit_Extender bit_extender_1
  assign bit_extender_2_out = {{20{Instr[31]}}, Instr[31]};  // Bit_Extender bit_extender_2
  Multiplexer #(.select(2), .width(32)) multiplexer_1 (
    .in0({bit_extender_2_out, Instr[30:20]}), .in1({Instr[31:12], {12{1'b0}}}),
    .in2({bit_extender_1_out, Instr[30:25], Instr[11:7]}), .out(Imm32));  // open: in3, sel

  // Notes on the sheet:
  //   I_immediate
  //   U_immediate
  //   S_immediate
endmodule

module Instruction_Mem (
  input  [31:0] Addr,
  output [31:0] Instr
);

  wire [15:0] bit_extender_1_out;

  Bit_Extender #(.in_width(32)) bit_extender_1 (.in(Addr), .out(bit_extender_1_out));
  ROM #(.addrWidth(16), .dataWidth(32)) rom_1 (.addr(bit_extender_1_out), .data(Instr));

  // Notes on the sheet:
  //   contents of rom_1 (hex, n*v repeats v):
  //   1400513 0 0 0 10000e7 0 0 0 c000e7 0 0 0 c00067 0 0 0 a50513 0 0 0 8067
endmodule

module Data_Memory (
  input  [31:0] Addr,
  input  WE,
  input  [3:0] ByteEnable,
  input  CLK,
  input  [31:0] WData,
  output [31:0] RData
);

  wire [15:0] bit_extender_1_out;

  Bit_Extender #(.in_width(32)) bit_extender_1 (.in(Addr), .out(bit_extender_1_out));
  RAM #(.addrWidth(16), .asyncread("true"), .byteenables("byteEnables"), .dataWidth(32), .\type ("nonvolatile")) ram_1 (
    .addr(bit_extender_1_out), .we(WE), .oe(1'b1), .clk(CLK), .din(WData), .dout(RData), .be3(ByteEnable[3]),
    .be2(ByteEnable[2]), .be1(ByteEnable[1]), .be0(ByteEnable[0]));
endmodule

module Control_Unit (
  input  [6:0] opcode,
  input  [2:0] funct3,
  output PCSrc,
  output [1:0] ImmSrc,
  output RegWrite,
  output ALUSrc,
  output MemWrite,
  output [1:0] ResultSrc,
  output ByteSrc
);

  wire and_1_out, and_2_out, comparator_4_eq, comparator_5_eq, comparator_7_eq, comparator_8_eq;

  Comparator #(.width(7)) comparator_1 (.a(7'b0010011), .b(opcode));  // open: gt, eq, lt
  Comparator #(.width(7)) comparator_2 (.a(7'b1100111), .b(opcode), .eq(PCSrc));  // open: gt, lt
  Comparator #(.width(7)) comparator_3 (.a(7'b0110111), .b(opcode), .eq(ImmSrc[0]));  // open: gt, lt
  Comparator #(.width(7)) comparator_4 (.a(7'b0110011), .b(opcode), .eq(comparator_4_eq));  // open: gt, lt
  Comparator #(.width(7)) comparator_5 (.a(7'b0000011), .b(opcode), .eq(comparator_5_eq));  // open: gt, lt
  Comparator #(.width(7)) comparator_6 (.a(7'b0100011), .b(opcode), .eq(ImmSrc[1]));  // open: gt, lt
  Comparator #(.width(3)) comparator_7 (.a(funct3), .b(3'b010), .eq(comparator_7_eq));  // open: gt, lt
  Comparator #(.width(3)) comparator_8 (.a(funct3), .b(3'b010), .eq(comparator_8_eq));  // open: gt, lt
  not not_1 (ALUSrc, comparator_4_eq);
  or or_1 (ResultSrc[0], PCSrc, ImmSrc[0]);
  or or_2 (ResultSrc[1], ImmSrc[0], comparator_5_eq);
  and and_1 (and_1_out, comparator_5_eq, comparator_7_eq);
  and and_2 (and_2_out, ImmSrc[1], comparator_8_eq);
  not not_2 (RegWrite, ImmSrc[1]);
  or or_3 (ByteSrc, and_1_out, and_2_out);

  assign MemWrite = ImmSrc[1];

  // Notes on the sheet:
  //   lw/lbu
  //   sw/sb
  //   addi
  //   jalr
  //   lui
  //   add
  //   lw
  //   sw
endmodule

module LUI_ADD_Instr_Mem (
  input  [31:0] Addr,
  output [31:0] Instr
);

  wire [5:0] bit_extender_1_out;

  Bit_Extender #(.in_width(32), .out_width(6)) bit_extender_1 (.in(Addr), .out(bit_extender_1_out));
  ROM #(.addrWidth(6), .dataWidth(32)) rom_1 (.addr(bit_extender_1_out), .data(Instr));

  // Notes on the sheet:
  //   contents of rom_1 (hex, n*v repeats v):
  //   5675b7 0 0 0 34000537 0 0 0 b504b3 0 0 0 628293 0 0 0 92a523 0 0 0 a2a403 0 0 0 52a303 0 0 0 52c603
  //   0 0 0 c28223 0 0 0 6284a3
endmodule

module ByteSelect (
  input  ByteSel,
  input  [31:0] RWord,
  output [31:0] WordSelected
);

  wire [31:0] bit_extender_1_out;

  assign bit_extender_1_out = {{24{1'b0}}, RWord[7:0]};  // Bit_Extender bit_extender_1
  Multiplexer #(.width(32)) multiplexer_1 (.in0(bit_extender_1_out), .in1(RWord), .out(WordSelected), .sel(ByteSel));
endmodule

module mem_instr_Mem (
  input  [31:0] Addr,
  output [31:0] Instr
);

  wire [23:0] bit_extender_1_out;

  Bit_Extender #(.in_width(32), .out_width(24)) bit_extender_1 (.in(Addr), .out(bit_extender_1_out));
  ROM #(.addrWidth(24), .dataWidth(32)) rom_1 (.addr(bit_extender_1_out), .data(Instr));

  // Notes on the sheet:
  //   contents of rom_1 (hex, n*v repeats v):
  //   413 52137 10113 10b7 22408093 80e7 fea12823 fe812e23 1437 40840413 ff014183 3401b3 1c183 ff114203
  //   440233 24203 4181b3 ff214203 440233 24203 4181b3 ff314203 440233 24203 4181b3 1237 40020213 320233
  //   24203 ffc12403 420233 420233 410233 a000193 fe312823 9c00193 fe312623 fec22203 20067 8067 ff410113
  //   100513 112423 10b7 21808093 80e7 fec10113 912423 494b7 6b048493 812623 112823 496b7 69068693 48413
  //   48713 fe012823 174183 fe3109a3 ff012183 fe812e23 fe312823 3d437 60040413 ff214203 420233 420233
  //   440233 22203 fe412623 ff114203 420233 420233 440233 22203 fe412423 ff014203 420233 420233 440233
  //   22203 fe412223 fed14183 fea14203 4181b3 fe714203 4181b3 fe312223 fee14183 feb14203 4181b3 fe3102a3
  //   fef14183 fe310323 fe412183 8237 20213 440433 ff314203 420233 420233 440233 22203 ffc12403 4181b3
  //   74503 350533 6a603 270713 468693 fe312a23 fec12423 31237 50020213 feb14183 4181b3 1c183 fe3103a3
  //   fea14183 4181b3 1c183 fe310323 fe914183 4181b3 1c183 fe3102a3 fe814183 4181b3 1c183 fe310223
  //   ff412183 fe412203 450533 150513 fea12823 fe812e23 1437 40840413 ff014183 3401b3 1c183 ff114203
  //   440233 24203 4181b3 ff214203 440233 24203 4181b3 ff314203 440233 24203 4181b3 1237 40020213 320233
  //   24503 ffc12403 e12223 d12023 1800093 80e7 412703 497b7 6c078793 12683 fee12823 fef12623 fe812e23
  //   fe912c23 1437 30040413 ff014183 340233 100193 320023 fec14183 3401b3 18023 24183 ff114483 940233
  //   100493 920023 fed14483 9404b3 48023 24483 9181b3 ff214483 940233 100493 920023 fee14483 9404b3 48023
  //   24483 9181b3 ff314483 940233 100493 920023 fef14483 9404b3 48023 24483 9181b3 1237 40020213 320233
  //   24203 ff812483 ffc12403 420233 420233 410233 37800193 fe312823 e000193 fe312623 fec22203 20067 49737
  //   67070713 72683 fe012823 14c203 fe4108a3 ff012203 4c503 450533 470713 e12023 fe312a23 fed12423 31237
  //   50020213 feb14183 4181b3 1c183 fe3103a3 fea14183 4181b3 1c183 fe310323 fe914183 4181b3 1c183
  //   fe3102a3 fe814183 4181b3 1c183 fe310223 ff412183 fe412203 450533 150513 fea12823 fe812e23 1437
  //   40840413 ff014183 3401b3 1c183 ff114203 440233 24203 4181b3 ff214203 440233 24203 4181b3 ff314203
  //   440233 24203 4181b3 1237 40020213 320233 24503 ffc12403 1800093 80e7 248493 497b7 6c078793 12703
  //   fe912823 fef12623 fe812e23 fe912c23 1437 30040413 ff014183 340233 100193 320023 fec14183 3401b3
  //   18023 24183 ff114483 940233 100493 920023 fed14483 9404b3 48023 24483 9181b3 ff214483 940233 100493
  //   920023 fee14483 9404b3 48023 24483 9181b3 ff314483 940233 100493 920023 fef14483 9404b3 48023 24483
  //   9181b3 1237 40020213 320233 24203 ff812483 ffc12403 420233 420233 410233 55c00193 fe312823 38000193
  //   fe312623 fec22203 20067 244683 144603 344703 444783 494b7 64048493 8*d686b3 fed12823 fec12623 116b7
  //   60068693 fe012223 ff314203 fe4102a3 fef14203 fe410223 fe412203 468233 24203 fe4105a3 ff214203
  //   fe4102a3 fee14203 fe410223 fe412203 468233 24203 fe410523 ff114203 fe4102a3 fed14203 fe410223
  //   fe412203 468233 24203 fe4104a3 ff014203 fe4102a3 fec14203 fe410223 fe412203 468233 24203 fe410423
  //   fe812683 4a503 fe012823 fee10923 fee12423 fe914203 fe4109a3 ff012703 fee12823 fed12623 11737
  //   60070713 fe012223 ff314203 fe4102a3 fef14203 fe410223 fe412203 470233 24203 fe4105a3 ff214203
  //   fe4102a3 fee14203 fe410223 fe412203 470233 24203 fe410523 ff114203 fe4102a3 fed14203 fe410223
  //   fe412203 470233 24203 fe4104a3 ff014203 fe4102a3 fec14203 fe410223 fe412203 470233 24203 fe410423
  //   fe812703 fe012823 fef109a3 ff012783 fef12823 fee12623 117b7 60078793 fe012223 ff314203 fe4102a3
  //   fef14203 fe410223 fe412203 478233 24203 fe4105a3 ff214203 fe4102a3 fee14203 fe410223 fe412203 478233
  //   24203 fe410523 ff114203 fe4102a3 fed14203 fe410223 fe412203 478233 24203 fe4104a3 ff014203 fe4102a3
  //   fec14203 fe410223 fe412203 478233 24203 fe410423 fe812783 fe312a23 fef12423 31237 50020213 feb14183
  //   4181b3 1c183 fe3103a3 fea14183 4181b3 1c183 fe310323 fe914183 4181b3 1c183 fe3102a3 fe814183 4181b3
  //   1c183 fe310223 ff412183 fe412203 450533 150513 fea12823 fe812e23 1437 40840413 ff014183 3401b3 1c183
  //   ff114203 440233 24203 4181b3 ff214203 440233 24203 4181b3 ff314203 440233 24203 4181b3 1237 400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
endmodule

module mem_data_Mem (
  input  [31:0] Addr,
  input  WE,
  input  [3:0] ByteEnable,
  input  CLK,
  input  [31:0] WData,
  output [31:0] RData
);

  wire [23:0] bit_extender_1_out;

  Bit_Extender #(.in_width(32), .out_width(24)) bit_extender_1 (.in(Addr), .out(bit_extender_1_out));
  RAM #(.addrWidth(24), .asyncread("true"), .byteenables("byteEnables"), .dataWidth(32), .\type ("nonvolatile")) ram_1 (
    .addr(bit_extender_1_out), .we(WE), .oe(1'b1), .clk(CLK), .din(WData), .dout(RData), .be3(ByteEnable[3]),
    .be2(ByteEnable[2]), .be1(ByteEnable[1]), .be0(ByteEnable[0]));
endmodule

module AddrDecoder (
  input  [31:0] Addr,
  output isVGA,
  output isMem
);

  wire comparator_1_eq, comparator_1_gt, comparator_2_lt, or_1_out;

  Comparator #(.width(32)) comparator_1 (
    .a(Addr), .b(32'h20000000), .gt(comparator_1_gt), .eq(comparator_1_eq));  // open: lt
  Comparator #(.width(32)) comparator_2 (.a(Addr), .b(32'h20040000), .lt(comparator_2_lt));  // open: gt, eq
  or or_1 (or_1_out, comparator_1_gt, comparator_1_eq);
  and and_1 (isVGA, or_1_out, comparator_2_lt);
  not not_1 (isMem, isVGA);
endmodule

module Addr2Coordinates (
  input  [31:0] Addr,
  output [7:0] x_coor,
  output [7:0] y_coor
);

  wire [31:0] and_1_out, shifter_1_out, shifter_2_out, subtractor_1_out;

  Subtractor #(.width(32)) subtractor_1 (.a(Addr), .b(32'h20000000), .out(subtractor_1_out));  // open: bin, bout
  Shifter #(.shift("lr"), .width(32)) shifter_1 (.in(subtractor_1_out), .\dist (5'b00010), .out(shifter_1_out));
  Shifter #(.shift("lr"), .width(32)) shifter_2 (.in(subtractor_1_out), .\dist (5'b01010), .out(shifter_2_out));
  assign and_1_out = shifter_1_out & 32'hff;  // AND_Gate and_1, 32 bits wide
  Bit_Extender #(.in_width(32), .out_width(8), .\type ("zero")) bit_extender_1 (.in(and_1_out), .out(x_coor));
  Bit_Extender #(.in_width(32), .out_width(8), .\type ("zero")) bit_extender_2 (.in(shifter_2_out), .out(y_coor));
endmodule
