// Logisim project sCPU.circ as structural Verilog: 3 circuits, main circuit main
module main (
  input  En,
  input  Clr
);

  wire and_1_out, button_1_out, comparator_1_eq, decoder_1_out0, decoder_1_out1, decoder_1_out2,
       decoder_1_out3, not_1_out, or_1_out;
  wire [1:0] multiplexer_3_out;
  wire [2:0] bit_extender_1_out;
  wire [3:0] counter_1_q, multiplexer_1_out, PC_q, rom_1_out;
  wire [7:0] adder_1_out, bit_extender_2_out, gpr_1_rdata1, gpr_1_rdata2, multiplexer_2_out, rom_1_out_2;

  Button button_1 (.out(button_1_out));
  Counter #(.width(4), .max('hf)) counter_1 (
    .count(En), .Q(counter_1_q), .clk(button_1_out), .clr(Clr));  // open: load, D, carry
  Multiplexer #(.width(4), .enable("false")) multiplexer_1 (
    .in0(counter_1_q), .in1(rom_1_out), .out(multiplexer_1_out), .sel(and_1_out));
  // Probe on PC_q
  Register #(.width(4)) PC (.D(multiplexer_1_out), .en(1'b1), .Q(PC_q), .clk(button_1_out));  // open: clr
  // Probe on {rom_1_out_2[7:6], rom_1_out, rom_1_out_2[1:0]}
  Bit_Extender #(.in_width(4), .out_width(3)) bit_extender_1 (.in(PC_q), .out(bit_extender_1_out));
  ROM rom_1 (.PC(bit_extender_1_out), .Out({rom_1_out_2[7:6], rom_1_out, rom_1_out_2[1:0]}));
  Decoder #(.select(2), .enable("false")) decoder_1 (
    .out0(decoder_1_out0), .out1(decoder_1_out1), .out2(decoder_1_out2), .out3(decoder_1_out3),
    .sel(rom_1_out_2[7:6]));
  assign bit_extender_2_out = {{4{1'b0}}, {rom_1_out[1:0], rom_1_out_2[1:0]}};  // Bit_Extender bit_extender_2
  and and_1 (and_1_out, decoder_1_out3, not_1_out);
  Multiplexer #(.width(8), .enable("false")) multiplexer_2 (
    .in0(adder_1_out), .in1(bit_extender_2_out), .out(multiplexer_2_out), .sel(decoder_1_out2));
  Multiplexer #(.width(2), .enable("false")) multiplexer_3 (
    .in0(rom_1_out[1:0]), .in1(2'b00), .out(multiplexer_3_out), .sel(decoder_1_out3));
  or or_1 (or_1_out, decoder_1_out0, decoder_1_out2);
  GPR gpr_1 (
    .wdata(multiplexer_2_out), .waddr(rom_1_out[3:2]), .wen(or_1_out), .Clk(button_1_out),
    .rdata1(gpr_1_rdata1), .raddr1(multiplexer_3_out), .raddr2(rom_1_out_2[1:0]), .rdata2(gpr_1_rdata2));
  not not_1 (not_1_out, comparator_1_eq);
  Comparator comparator_1 (.a(gpr_1_rdata1), .b(gpr_1_rdata2), .eq(comparator_1_eq));  // open: gt, lt
  Adder adder_1 (.a(gpr_1_rdata1), .b(gpr_1_rdata2), .out(adder_1_out), .cin(1'b0));  // open: cout
endmodule

module ROM (
  input  [2:0] PC,
  output [7:0] Out
);

  Multiplexer #(.select(3), .width(8), .enable("false")) multiplexer_1 (
    .in0(8'h8a), .in1(8'h90), .in2(8'ha0), .in3(8'hb1), .in4(8'h17), .in5(8'h29), .in6(8'hd1), .in7(8'hdf),
    .out(Out), .sel(PC));
endmodule

module GPR (
  input  [7:0] wdata,
  input  [1:0] waddr,
  input  wen,
  input  Clk,
  input  [1:0] raddr1,
  input  [1:0] raddr2,
  output [7:0] rdata2,
  output [7:0] rdata1
);

  wire and_1_out, and_2_out, and_3_out, and_4_out, and_5_out, and_6_out, and_7_out, and_8_out, and_10_out,
       and_11_out, and_12_out, and_13_out, and_14_out, and_15_out, and_16_out, and_17_out, and_18_out,
       and_19_out, and_20_out, and_21_out, and_22_out, and_23_out, and_24_out, and_25_out, and_26_out,
       and_27_out, and_28_out, and_29_out, and_30_out, and_31_out, and_32_out, and_33_out, and_34_out,
       and_35_out, and_36_out, and_37_out, and_38_out, and_39_out, and_40_out, and_41_out, and_42_out,
       and_43_out, and_44_out, and_45_out, and_46_out, and_47_out, and_48_out, and_49_out, and_50_out,
       and_51_out, and_52_out, and_53_out, and_54_out, and_55_out, and_56_out, and_57_out, and_58_out,
       and_59_out, and_60_out, and_61_out, and_62_out, and_63_out, and_64_out, and_65_out, and_66_out,
       and_67_out, and_68_out, d_ff_1_q, d_ff_2_q, d_ff_3_q, d_ff_4_q, d_ff_5_q, d_ff_6_q, d_ff_7_q,
       d_ff_8_q, d_ff_9_q, d_ff_10_q, d_ff_11_q, d_ff_12_q, d_ff_13_q, d_ff_14_q, d_ff_15_q, d_ff_16_q,
       d_ff_17_q, d_ff_18_q, d_ff_19_q, d_ff_20_q, d_ff_21_q, d_ff_22_q, d_ff_23_q, d_ff_24_q, d_ff_25_q,
       d_ff_26_q, d_ff_27_q, d_ff_28_q, d_ff_29_q, d_ff_30_q, d_ff_31_q, d_ff_32_q, decoder_1_out0,
       decoder_1_out1, decoder_1_out2, decoder_1_out3, decoder_2_out0, decoder_2_out1, decoder_2_out2,
       decoder_2_out3, decoder_3_out0, decoder_3_out1, decoder_3_out2, decoder_3_out3;

  Decoder #(.select(2), .enable("false")) decoder_1 (
    .out0(decoder_1_out0), .out1(decoder_1_out1), .out2(decoder_1_out2), .out3(decoder_1_out3), .sel(waddr));
  Decoder #(.select(2), .enable("false")) decoder_2 (
    .out0(decoder_2_out0), .out1(decoder_2_out1), .out2(decoder_2_out2), .out3(decoder_2_out3), .sel(raddr1));
  Decoder #(.select(2), .enable("false")) decoder_3 (
    .out0(decoder_3_out0), .out1(decoder_3_out1), .out2(decoder_3_out2), .out3(decoder_3_out3), .sel(raddr2));
  and and_1 (and_1_out, decoder_1_out0, wen);
  and and_2 (and_2_out, decoder_1_out1, wen);
  and and_3 (and_3_out, decoder_1_out2, wen);
  and and_4 (and_4_out, decoder_1_out3, wen);
  D_Flip_Flop d_ff_1 (.clk(Clk), .D(wdata[7]), .Q(d_ff_1_q), .en(and_1_out));  // open: Qn, preset, reset
  D_Flip_Flop d_ff_2 (.clk(Clk), .D(wdata[7]), .Q(d_ff_2_q), .en(and_2_out));  // open: Qn, preset, reset
  D_Flip_Flop d_ff_3 (.clk(Clk), .D(wdata[7]), .Q(d_ff_3_q), .en(and_3_out));  // open: Qn, preset, reset
  D_Flip_Flop d_ff_4 (.clk(Clk), .D(wdata[7]), .Q(d_ff_4_q), .en(and_4_out));  // open: Qn, preset, reset
  or or_1 (rdata2[7], and_7_out, and_6_out, and_5_out);
  and and_5 (and_5_out, d_ff_1_q, decoder_3_out0);
  and and_6 (and_6_out, d_ff_2_q, decoder_3_out1);
  and and_7 (and_7_out, d_ff_3_q, decoder_3_out2);
  and and_8 (and_8_out, decoder_2_out3, d_ff_4_q);
  and and_9 (decoder_2_out0, d_ff_4_q, decoder_3_out3);
  and and_10 (and_10_out, decoder_2_out0, d_ff_1_q);
  and and_11 (and_11_out, decoder_2_out1, d_ff_2_q);
  and and_12 (and_12_out, decoder_2_out2, d_ff_3_q);
  or or_2 (rdata1[7], and_8_out, and_12_out, and_11_out, and_10_out);
  D_Flip_Flop d_ff_5 (.clk(Clk), .D(wdata[6]), .Q(d_ff_5_q), .en(and_1_out));  // open: Qn, preset, reset
  D_Flip_Flop d_ff_6 (.clk(Clk), .D(wdata[6]), .Q(d_ff_6_q), .en(and_2_out));  // open: Qn, preset, reset
  D_Flip_Flop d_ff_7 (.clk(Clk), .D(wdata[6]), .Q(d_ff_7_q), .en(and_3_out));  // open: Qn, preset, reset
  D_Flip_Flop d_ff_8 (.clk(Clk), .D(wdata[6]), .Q(d_ff_8_q), .en(and_4_out));  // open: Qn, preset, reset
  or or_3 (rdata2[6], and_17_out, and_15_out, and_14_out, and_13_out);
  and and_13 (and_13_out, d_ff_5_q, decoder_3_out0);
  and and_14 (and_14_out, d_ff_6_q, decoder_3_out1);
  and and_15 (and_15_out, d_ff_7_q, decoder_3_out2);
  and and_16 (and_16_out, decoder_2_out3, d_ff_8_q);
  and and_17 (and_17_out, d_ff_8_q, decoder_3_out3);
  and and_18 (and_18_out, decoder_2_out0, d_ff_5_q);
  and and_19 (and_19_out, decoder_2_out1, d_ff_6_q);
  and and_20 (and_20_out, decoder_2_out2, d_ff_7_q);
  or or_4 (rdata1[6], and_16_out, and_20_out, and_19_out, and_18_out);
  or or_5 (rdata2[5], and_21_out, and_26_out, and_24_out, and_22_out);
  D_Flip_Flop d_ff_9 (.clk(Clk), .D(wdata[5]), .Q(d_ff_9_q), .en(and_1_out));  // open: Qn, preset, reset
  D_Flip_Flop d_ff_10 (.clk(Clk), .D(wdata[5]), .Q(d_ff_10_q), .en(and_2_out));  // open: Qn, preset, reset
  D_Flip_Flop d_ff_11 (.clk(Clk), .D(wdata[5]), .Q(d_ff_11_q), .en(and_3_out));  // open: Qn, preset, reset
  D_Flip_Flop d_ff_12 (.clk(Clk), .D(wdata[5]), .Q(d_ff_12_q), .en(and_4_out));  // open: Qn, preset, reset
  and and_21 (and_21_out, d_ff_12_q, decoder_3_out3);
  and and_22 (and_22_out, d_ff_9_q, decoder_3_out0);
  and and_23 (and_23_out, decoder_2_out1, d_ff_10_q);
  and and_24 (and_24_out, d_ff_10_q, decoder_3_out1);
  and and_25 (and_25_out, decoder_2_out2, d_ff_11_q);
  and and_26 (and_26_out, d_ff_11_q, decoder_3_out2);
  and and_27 (and_27_out, decoder_2_out3, d_ff_12_q);
  or or_6 (rdata1[5], and_27_out, and_25_out, and_23_out, and_28_out);
  and and_28 (and_28_out, decoder_2_out0, d_ff_9_q);
  or or_7 (rdata2[4], and_31_out, and_30_out, and_29_out, and_33_out);
  D_Flip_Flop d_ff_13 (.clk(Clk), .D(wdata[4]), .Q(d_ff_13_q), .en(and_1_out));  // open: Qn, preset, reset
  D_Flip_Flop d_ff_14 (.clk(Clk), .D(wdata[4]), .Q(d_ff_14_q), .en(and_2_out));  // open: Qn, preset, reset
  and and_29 (and_29_out, d_ff_14_q, decoder_3_out1);
  D_Flip_Flop d_ff_15 (.clk(Clk), .D(wdata[4]), .Q(d_ff_15_q), .en(and_3_out));  // open: Qn, preset, reset
  and and_30 (and_30_out, d_ff_15_q, decoder_3_out2);
  D_Flip_Flop d_ff_16 (.clk(Clk), .D(wdata[4]), .Q(d_ff_16_q), .en(and_4_out));  // open: Qn, preset, reset
  and and_31 (and_31_out, d_ff_16_q, decoder_3_out3);
  and and_32 (and_32_out, decoder_2_out0, d_ff_13_q);
  and and_33 (and_33_out, d_ff_13_q, decoder_3_out0);
  and and_34 (and_34_out, decoder_2_out1, d_ff_14_q);
  and and_35 (and_35_out, decoder_2_out2, d_ff_15_q);
  and and_36 (and_36_out, decoder_2_out3, d_ff_16_q);
  or or_8 (rdata1[4], and_36_out, and_35_out, and_34_out, and_32_out);
  D_Flip_Flop d_ff_17 (.clk(Clk), .D(wdata[3]), .Q(d_ff_17_q), .en(and_1_out));  // open: Qn, preset, reset
  D_Flip_Flop d_ff_18 (.clk(Clk), .D(wdata[3]), .Q(d_ff_18_q), .en(and_2_out));  // open: Qn, preset, reset
  D_Flip_Flop d_ff_19 (.clk(Clk), .D(wdata[3]), .Q(d_ff_19_q), .en(and_3_out));  // open: Qn, preset, reset
  D_Flip_Flop d_ff_20 (.clk(Clk), .D(wdata[3]), .Q(d_ff_20_q), .en(and_4_out));  // open: Qn, preset, reset
  or or_9 (rdata2[3], and_42_out, and_40_out, and_38_out, and_37_out);
  and and_37 (and_37_out, d_ff_17_q, decoder_3_out0);
  and and_38 (and_38_out, d_ff_18_q, decoder_3_out1);
  and and_39 (and_39_out, decoder_2_out2, d_ff_19_q);
  and and_40 (and_40_out, d_ff_19_q, decoder_3_out2);
  and and_41 (and_41_out, decoder_2_out3, d_ff_20_q);
  and and_42 (and_42_out, d_ff_20_q, decoder_3_out3);
  and and_43 (and_43_out, decoder_2_out0, d_ff_17_q);
  and and_44 (and_44_out, decoder_2_out1, d_ff_18_q);
  or or_10 (rdata1[3], and_41_out, and_39_out, and_44_out, and_43_out);
  or or_11 (rdata2[2], and_45_out, and_51_out, and_49_out, and_47_out);
  D_Flip_Flop d_ff_21 (.clk(Clk), .D(wdata[2]), .Q(d_ff_21_q), .en(and_1_out));  // open: Qn, preset, reset
  D_Flip_Flop d_ff_22 (.clk(Clk), .D(wdata[2]), .Q(d_ff_22_q), .en(and_2_out));  // open: Qn, preset, reset
  D_Flip_Flop d_ff_23 (.clk(Clk), .D(wdata[2]), .Q(d_ff_23_q), .en(and_3_out));  // open: Qn, preset, reset
  D_Flip_Flop d_ff_24 (.clk(Clk), .D(wdata[2]), .Q(d_ff_24_q), .en(and_4_out));  // open: Qn, preset, reset
  and and_45 (and_45_out, d_ff_24_q, decoder_3_out3);
  and and_46 (and_46_out, decoder_2_out0, d_ff_21_q);
  and and_47 (and_47_out, d_ff_21_q, decoder_3_out0);
  and and_48 (and_48_out, decoder_2_out1, d_ff_22_q);
  and and_49 (and_49_out, d_ff_22_q, decoder_3_out1);
  and and_50 (and_50_out, decoder_2_out2, d_ff_23_q);
  and and_51 (and_51_out, d_ff_23_q, decoder_3_out2);
  and and_52 (and_52_out, decoder_2_out3, d_ff_24_q);
  or or_12 (rdata1[2], and_52_out, and_50_out, and_48_out, and_46_out);
  or or_13 (rdata2[1], and_55_out, and_54_out, and_53_out, and_57_out);
  D_Flip_Flop d_ff_25 (.clk(Clk), .D(wdata[1]), .Q(d_ff_25_q), .en(and_1_out));  // open: Qn, preset, reset
  D_Flip_Flop d_ff_26 (.clk(Clk), .D(wdata[1]), .Q(d_ff_26_q), .en(and_2_out));  // open: Qn, preset, reset
  and and_53 (and_53_out, d_ff_26_q, decoder_3_out1);
  D_Flip_Flop d_ff_27 (.clk(Clk), .D(wdata[1]), .Q(d_ff_27_q), .en(and_3_out));  // open: Qn, preset, reset
  and and_54 (and_54_out, d_ff_27_q, decoder_3_out2);
  D_Flip_Flop d_ff_28 (.clk(Clk), .D(wdata[1]), .Q(d_ff_28_q), .en(and_4_out));  // open: Qn, preset, reset
  and and_55 (and_55_out, d_ff_28_q, decoder_3_out3);
  and and_56 (and_56_out, decoder_2_out0, d_ff_25_q);
  and and_57 (and_57_out, d_ff_25_q, decoder_3_out0);
  and and_58 (and_58_out, decoder_2_out1, d_ff_26_q);
  and and_59 (and_59_out, decoder_2_out2, d_ff_27_q);
  and and_60 (and_60_out, decoder_2_out3, d_ff_28_q);
  or or_14 (rdata1[1], and_60_out, and_59_out, and_58_out, and_56_out);
  or or_15 (rdata2[0], and_64_out, and_62_out, and_61_out, and_66_out);
  D_Flip_Flop d_ff_29 (.clk(Clk), .D(wdata[0]), .Q(d_ff_29_q), .en(and_1_out));  // open: Qn, preset, reset
  D_Flip_Flop d_ff_30 (.clk(Clk), .D(wdata[0]), .Q(d_ff_30_q), .en(and_2_out));  // open: Qn, preset, reset
  and and_61 (and_61_out, d_ff_30_q, decoder_3_out1);
  D_Flip_Flop d_ff_31 (.clk(Clk), .D(wdata[0]), .Q(d_ff_31_q), .en(and_3_out));  // open: Qn, preset, reset
  and and_62 (and_62_out, d_ff_31_q, decoder_3_out2);
  and and_63 (and_63_out, decoder_2_out3, d_ff_32_q);
  D_Flip_Flop d_ff_32 (.clk(Clk), .D(wdata[0]), .Q(d_ff_32_q), .en(and_4_out));  // open: Qn, preset, reset
  and and_64 (and_64_out, d_ff_32_q, decoder_3_out3);
  and and_65 (and_65_out, decoder_2_out0, d_ff_29_q);
  and and_66 (and_66_out, d_ff_29_q, decoder_3_out0);
  and and_67 (and_67_out, decoder_2_out1, d_ff_30_q);
  and and_68 (and_68_out, decoder_2_out2, d_ff_31_q);
  or or_16 (rdata1[0], and_63_out, and_68_out, and_67_out, and_65_out);
endmodule
