// Logisim project sCPU_logisim_v4.1.circ as structural Verilog: 7 circuits, main circuit main
module main (
  input  Rst_PC
);

  wire and_1_out, Clk_out, comparator_1_eq, decoder_1_out0, decoder_1_out1, decoder_1_out2, decoder_1_out3,
       not_1_out, or_1_out;
  wire [1:0] multiplexer_2_out;
  wire [2:0] adder_1_out, bit_extender_1_out;
  wire [3:0] bit_extender_2_out, instr_rom_1_instr_3, multiplexer_1_out, PC_q;
  wire [3:2] instr_rom_1_instr;
  wire [7:0] adder_2_out, bit_extender_3_out, gpr_1_rdata1, gpr_1_rdata2, multiplexer_3_out;
  wire [7:6] instr_rom_1_instr_2;

  Button Clk (.out(Clk_out));
  Multiplexer #(.width(4)) multiplexer_1 (
    .in0(bit_extender_2_out), .in1({instr_rom_1_instr, instr_rom_1_instr_3[3:2]}), .out(multiplexer_1_out),
    .sel(and_1_out));
  Register #(.width(4)) PC (.D(multiplexer_1_out), .en(1'b1), .clk(Clk_out), .Q(PC_q), .clr(Rst_PC));
  // Probe on bit_extender_1_out
  Bit_Extender #(.in_width(4), .out_width(3), .\type ("zero")) bit_extender_1 (.in(PC_q), .out(bit_extender_1_out));
  Adder #(.width(3)) adder_1 (.a(bit_extender_1_out), .b(3'b001), .out(adder_1_out));  // open: cin, cout
  assign bit_extender_2_out = {{1{1'b0}}, adder_1_out};  // Bit_Extender bit_extender_2
  // Probe on {instr_rom_1_instr_2, instr_rom_1_instr, instr_rom_1_instr_3}
  Instr_ROM instr_rom_1 (
    .instr_addr(bit_extender_1_out), .instr({instr_rom_1_instr_2, instr_rom_1_instr, instr_rom_1_instr_3}));
  Decoder #(.enable("false"), .select(2)) decoder_1 (
    .out0(decoder_1_out0), .out1(decoder_1_out1), .out2(decoder_1_out2), .out3(decoder_1_out3),
    .sel(instr_rom_1_instr_2));
  and and_1 (and_1_out, decoder_1_out3, not_1_out);
  Multiplexer #(.width(2)) multiplexer_2 (
    .in0(instr_rom_1_instr_3[3:2]), .in1(2'b00), .out(multiplexer_2_out), .sel(decoder_1_out3));
  assign bit_extender_3_out = {{4{1'b0}}, instr_rom_1_instr_3};  // Bit_Extender bit_extender_3
  or or_1 (or_1_out, decoder_1_out0, decoder_1_out2);
  Multiplexer #(.width(8)) multiplexer_3 (
    .in0(adder_2_out), .in1(bit_extender_3_out), .out(multiplexer_3_out), .sel(decoder_1_out2));
  GPR gpr_1 (
    .wdata(multiplexer_3_out), .waddr(instr_rom_1_instr), .wen(or_1_out), .Clk(Clk_out),
    .raddr1(multiplexer_2_out), .raddr2(instr_rom_1_instr_3[1:0]), .rdata1(gpr_1_rdata1),
    .rdata2(gpr_1_rdata2));
  Adder adder_2 (.a(gpr_1_rdata1), .b(gpr_1_rdata2), .out(adder_2_out));  // open: cin, cout
  Comparator comparator_1 (.a(gpr_1_rdata1), .b(gpr_1_rdata2), .eq(comparator_1_eq));  // open: gt, lt
  not not_1 (not_1_out, comparator_1_eq);
endmodule

module Instr_ROM (
  input  [2:0] instr_addr,
  output [7:0] instr
);

  Multiplexer #(.select(3), .width(8)) multiplexer_1 (
    .in0(8'h8a), .in1(8'h90), .in2(8'ha0), .in3(8'hb1), .in4(8'h17), .in5(8'h29), .in6(8'hd1), .in7(8'hdf),
    .out(instr), .sel(instr_addr));
endmodule

module GPR (
  input  [7:0] wdata,
  input  [1:0] waddr,
  input  wen,
  input  Clk,
  input  [1:0] raddr1,
  input  [1:0] raddr2,
  output [7:0] rdata1,
  output [7:0] rdata2
);

  wire and_1_out, and_2_out, and_3_out, and_4_out, decoder_1_out0, decoder_1_out1, decoder_1_out2,
       decoder_1_out3;
  wire [7:0] R0_q, R1_q, R2_q, R3_q;

  Decoder #(.enable("false"), .select(2)) decoder_1 (
    .out0(decoder_1_out0), .out1(decoder_1_out1), .out2(decoder_1_out2), .out3(decoder_1_out3), .sel(waddr));
  and and_1 (and_1_out, decoder_1_out0, wen);
  and and_2 (and_2_out, decoder_1_out1, wen);
  and and_3 (and_3_out, decoder_1_out2, wen);
  and and_4 (and_4_out, decoder_1_out3, wen);
  Register R0 (.D(wdata), .en(and_1_out), .clk(Clk), .Q(R0_q));  // open: clr
  Register R1 (.D(wdata), .en(and_2_out), .clk(Clk), .Q(R1_q));  // open: clr
  Register R2 (.D(wdata), .en(and_3_out), .clk(Clk), .Q(R2_q));  // open: clr
  Register R3 (.D(wdata), .en(and_4_out), .clk(Clk), .Q(R3_q));  // open: clr
  // Probe on R0_q
  // Probe on R1_q
  // Probe on R2_q
  // Probe on R3_q
  Multiplexer #(.select(2), .width(8)) multiplexer_1 (
    .in0(R0_q), .in1(R1_q), .in2(R2_q), .in3(R3_q), .out(rdata1), .sel(raddr1));
  Multiplexer #(.select(2), .width(8)) multiplexer_2 (
    .in0(R0_q), .in1(R1_q), .in2(R2_q), .in3(R3_q), .out(rdata2), .sel(raddr2));
endmodule

module Odd_sum_in_10 (
  input  Rst_PC
);

  wire and_1_out, Clk_out, comparator_1_eq, decoder_1_out0, decoder_1_out1, decoder_1_out2, decoder_1_out3,
       not_1_out, or_1_out;
  wire [1:0] multiplexer_2_out;
  wire [2:0] adder_1_out, bit_extender_1_out;
  wire [3:0] bit_extender_2_out, instr_rom_odd_sum_1_instr_3, multiplexer_1_out, PC_q;
  wire [3:2] instr_rom_odd_sum_1_instr;
  wire [7:0] adder_2_out, bit_extender_3_out, gpr_1_rdata1, gpr_1_rdata2, multiplexer_3_out;
  wire [7:6] instr_rom_odd_sum_1_instr_2;

  Button Clk (.out(Clk_out));
  Multiplexer #(.width(4)) multiplexer_1 (
    .in0(bit_extender_2_out), .in1({instr_rom_odd_sum_1_instr, instr_rom_odd_sum_1_instr_3[3:2]}),
    .out(multiplexer_1_out), .sel(and_1_out));
  Register #(.width(4)) PC (.D(multiplexer_1_out), .en(1'b1), .clk(Clk_out), .Q(PC_q), .clr(Rst_PC));
  // Probe on bit_extender_1_out
  Bit_Extender #(.in_width(4), .out_width(3), .\type ("zero")) bit_extender_1 (.in(PC_q), .out(bit_extender_1_out));
  Adder #(.width(3)) adder_1 (.a(bit_extender_1_out), .b(3'b001), .out(adder_1_out));  // open: cin, cout
  assign bit_extender_2_out = {{1{1'b0}}, adder_1_out};  // Bit_Extender bit_extender_2
  // Probe on {instr_rom_odd_sum_1_instr_2, instr_rom_odd_sum_1_instr, instr_rom_odd_sum_1_instr_3}
  Instr_ROM_odd_sum instr_rom_odd_sum_1 (
    .instr_addr(bit_extender_1_out),
    .instr({instr_rom_odd_sum_1_instr_2, instr_rom_odd_sum_1_instr, instr_rom_odd_sum_1_instr_3}));
  Decoder #(.enable("false"), .select(2)) decoder_1 (
    .out0(decoder_1_out0), .out1(decoder_1_out1), .out2(decoder_1_out2), .out3(decoder_1_out3),
    .sel(instr_rom_odd_sum_1_instr_2));
  and and_1 (and_1_out, decoder_1_out3, not_1_out);
  Multiplexer #(.width(2)) multiplexer_2 (
    .in0(instr_rom_odd_sum_1_instr_3[3:2]), .in1(2'b00), .out(multiplexer_2_out), .sel(decoder_1_out3));
  assign bit_extender_3_out = {{4{1'b0}}, instr_rom_odd_sum_1_instr_3};  // Bit_Extender bit_extender_3
  or or_1 (or_1_out, decoder_1_out0, decoder_1_out2);
  Multiplexer #(.width(8)) multiplexer_3 (
    .in0(adder_2_out), .in1(bit_extender_3_out), .out(multiplexer_3_out), .sel(decoder_1_out2));
  GPR gpr_1 (
    .wdata(multiplexer_3_out), .waddr(instr_rom_odd_sum_1_instr), .wen(or_1_out), .Clk(Clk_out),
    .raddr1(multiplexer_2_out), .raddr2(instr_rom_odd_sum_1_instr_3[1:0]), .rdata1(gpr_1_rdata1),
    .rdata2(gpr_1_rdata2));
  Adder adder_2 (.a(gpr_1_rdata1), .b(gpr_1_rdata2), .out(adder_2_out));  // open: cin, cout
  Comparator comparator_1 (.a(gpr_1_rdata1), .b(gpr_1_rdata2), .eq(comparator_1_eq));  // open: gt, lt
  not not_1 (not_1_out, comparator_1_eq);
endmodule

module Instr_ROM_odd_sum (
  input  [2:0] instr_addr,
  output [7:0] instr
);

  Multiplexer #(.select(3), .width(8)) multiplexer_1 (
    .in0(8'h8b), .in1(8'h91), .in2(8'ha0), .in3(8'hb2), .in4(8'h29), .in5(8'h17), .in6(8'hd1), .in7(8'hdf),
    .out(instr), .sel(instr_addr));
endmodule

module Instr_ROM_plus_display_instr (
  input  [2:0] instr_addr,
  output [7:0] instr
);

  Multiplexer #(.select(3), .width(8)) multiplexer_1 (
    .in0(8'h8a), .in1(8'h90), .in2(8'ha0), .in3(8'hb1), .in4(8'h17), .in5(8'h29), .in6(8'hd1), .in7(8'h42),
    .out(instr), .sel(instr_addr));
endmodule

module Sum_in_10_plus_display (
  input  Rst_PC
);

  wire and_1_out, Clk_out, comparator_1_eq, decoder_1_out0, decoder_1_out1, decoder_1_out2, decoder_1_out3,
       display_4_bits_7_seg_1_y0, display_4_bits_7_seg_1_y1, display_4_bits_7_seg_1_y2,
       display_4_bits_7_seg_1_y3, display_4_bits_7_seg_1_y4, display_4_bits_7_seg_1_y5,
       display_4_bits_7_seg_1_y6, display_4_bits_7_seg_1_y7, display_4_bits_7_seg_2_y0,
       display_4_bits_7_seg_2_y1, display_4_bits_7_seg_2_y2, display_4_bits_7_seg_2_y3,
       display_4_bits_7_seg_2_y4, display_4_bits_7_seg_2_y5, display_4_bits_7_seg_2_y6,
       display_4_bits_7_seg_2_y7, not_1_out, or_1_out;
  wire [1:0] multiplexer_2_out;
  wire [2:0] adder_1_out, bit_extender_1_out;
  wire [3:0] bit_extender_2_out, controlled_buffer_1_out, controlled_buffer_2_out, gpr_1_rdata2,
       gpr_1_rdata2_2, instr_rom_plus_display_instr_1_instr_3, multiplexer_1_out, PC_q;
  wire [3:2] instr_rom_plus_display_instr_1_instr;
  wire [7:0] adder_2_out, bit_extender_3_out, gpr_1_rdata1, multiplexer_3_out;
  wire [7:6] instr_rom_plus_display_instr_1_instr_2;

  Button Clk (.out(Clk_out));
  Multiplexer #(.width(4)) multiplexer_1 (
    .in0(bit_extender_2_out),
    .in1({instr_rom_plus_display_instr_1_instr, instr_rom_plus_display_instr_1_instr_3[3:2]}),
    .out(multiplexer_1_out), .sel(and_1_out));
  Register #(.width(4)) PC (.D(multiplexer_1_out), .en(1'b1), .clk(Clk_out), .Q(PC_q), .clr(Rst_PC));
  // Probe on bit_extender_1_out
  Bit_Extender #(.in_width(4), .out_width(3), .\type ("zero")) bit_extender_1 (.in(PC_q), .out(bit_extender_1_out));
  Adder #(.width(3)) adder_1 (.a(bit_extender_1_out), .b(3'b001), .out(adder_1_out));  // open: cin, cout
  assign bit_extender_2_out = {{1{1'b0}}, adder_1_out};  // Bit_Extender bit_extender_2
  // Probe on {instr_rom_plus_display_instr_1_instr_2, instr_rom_plus_display_instr_1_instr, instr_rom_plus_display_instr_1_instr_3}
  Instr_ROM_plus_display_instr instr_rom_plus_display_instr_1 (
    .instr_addr(bit_extender_1_out),
    .instr({instr_rom_plus_display_instr_1_instr_2, instr_rom_plus_display_instr_1_instr, instr_rom_plus_display_instr_1_instr_3}));
  LED led_1 (.in(decoder_1_out1));
  Decoder #(.enable("false"), .select(2)) decoder_1 (
    .out0(decoder_1_out0), .out1(decoder_1_out1), .out2(decoder_1_out2), .out3(decoder_1_out3),
    .sel(instr_rom_plus_display_instr_1_instr_2));
  and and_1 (and_1_out, decoder_1_out3, not_1_out);
  Multiplexer #(.width(2)) multiplexer_2 (
    .in0(instr_rom_plus_display_instr_1_instr_3[3:2]), .in1(2'b00), .out(multiplexer_2_out),
    .sel(decoder_1_out3));
  assign bit_extender_3_out = {{4{1'b0}}, instr_rom_plus_display_instr_1_instr_3};  // Bit_Extender bit_extender_3
  or or_1 (or_1_out, decoder_1_out0, decoder_1_out2);
  Multiplexer #(.width(8)) multiplexer_3 (
    .in0(adder_2_out), .in1(bit_extender_3_out), .out(multiplexer_3_out), .sel(decoder_1_out2));
  assign controlled_buffer_1_out = decoder_1_out1 ? gpr_1_rdata2_2 : 4'bz;  // Controlled_Buffer controlled_buffer_1
  assign controlled_buffer_2_out = decoder_1_out1 ? gpr_1_rdata2 : 4'bz;  // Controlled_Buffer controlled_buffer_2
  display_4_bits_7_seg display_4_bits_7_seg_1 (
    .Data(controlled_buffer_1_out), .Y0(display_4_bits_7_seg_1_y0), .Y1(display_4_bits_7_seg_1_y1),
    .Y2(display_4_bits_7_seg_1_y2), .Y3(display_4_bits_7_seg_1_y3), .Y4(display_4_bits_7_seg_1_y4),
    .Y5(display_4_bits_7_seg_1_y5), .Y6(display_4_bits_7_seg_1_y6), .Y7(display_4_bits_7_seg_1_y7));
  display_4_bits_7_seg display_4_bits_7_seg_2 (
    .Data(controlled_buffer_2_out), .Y0(display_4_bits_7_seg_2_y0), .Y1(display_4_bits_7_seg_2_y1),
    .Y2(display_4_bits_7_seg_2_y2), .Y3(display_4_bits_7_seg_2_y3), .Y4(display_4_bits_7_seg_2_y4),
    .Y5(display_4_bits_7_seg_2_y5), .Y6(display_4_bits_7_seg_2_y6), .Y7(display_4_bits_7_seg_2_y7));
  GPR gpr_1 (
    .wdata(multiplexer_3_out), .waddr(instr_rom_plus_display_instr_1_instr), .wen(or_1_out), .Clk(Clk_out),
    .raddr1(multiplexer_2_out), .raddr2(instr_rom_plus_display_instr_1_instr_3[1:0]), .rdata1(gpr_1_rdata1),
    .rdata2({gpr_1_rdata2_2, gpr_1_rdata2}));
  _7_Segment_Display u_7_segment_display_1 (
    .g(display_4_bits_7_seg_1_y0), .f(display_4_bits_7_seg_1_y1), .a(display_4_bits_7_seg_1_y2),
    .b(display_4_bits_7_seg_1_y3), .e(display_4_bits_7_seg_1_y4), .d(display_4_bits_7_seg_1_y5),
    .c(display_4_bits_7_seg_1_y6), .dp(display_4_bits_7_seg_1_y7));
  _7_Segment_Display u_7_segment_display_2 (
    .g(display_4_bits_7_seg_2_y0), .f(display_4_bits_7_seg_2_y1), .a(display_4_bits_7_seg_2_y2),
    .b(display_4_bits_7_seg_2_y3), .e(display_4_bits_7_seg_2_y4), .d(display_4_bits_7_seg_2_y5),
    .c(display_4_bits_7_seg_2_y6), .dp(display_4_bits_7_seg_2_y7));
  Adder adder_2 (.a(gpr_1_rdata1), .b({gpr_1_rdata2_2, gpr_1_rdata2}), .out(adder_2_out));  // open: cin, cout
  Comparator comparator_1 (.a(gpr_1_rdata1), .b({gpr_1_rdata2_2, gpr_1_rdata2}), .eq(comparator_1_eq));  // open: gt, lt
  not not_1 (not_1_out, comparator_1_eq);
endmodule
